// Logisim project lab1.3.circ as structural Verilog: 1 circuit, main circuit main
module main (
  input  D0,
  input  D1,
  input  S,
  output Y
);

  wire NAND0_out, NAND1_out, NAND2_out;

  // Probe on S
  nand NAND0 (NAND0_out, S, S);
  // Probe on NAND0_out
  nand NAND1 (NAND1_out, D0, NAND0_out);
  nand NAND3 (Y, NAND1_out, NAND2_out);
  nand NAND2 (NAND2_out, S, D1);

  // Notes on the sheet:
  //   输入引脚
  //   请勿修改引脚名称及电路封装外观
  //   提示：使用独立逻辑门实现二选一多路选择器，禁止直接使用选择器组件。
  //   输出引脚
endmodule
