// Logisim project lab1.5.circ as structural Verilog: 2 circuits, main circuit 4-1MUX
module _4_1MUX (
  input  D0,
  input  D1,
  input  D2,
  input  D3,
  input  S0,
  input  S1,
  output Y
);

  wire n2_1mux_1_y, n2_1mux_2_y;

  _2_1MUX u_2_1mux_1 (.D0(D0), .D1(D1), .S(S0), .Y(n2_1mux_1_y));
  _2_1MUX u_2_1mux_2 (.D0(D2), .D1(D3), .S(S0), .Y(n2_1mux_2_y));
  _2_1MUX u_2_1mux_3 (.D0(n2_1mux_1_y), .D1(n2_1mux_2_y), .S(S1), .Y(Y));

  // Notes on the sheet:
  //   输入引脚
  //   请勿修改引脚名称、电路名称及电路封装外观
  //   提示：使用二选一多路选择器子电路级联实现四选一多路选择器，禁止直接使用多路选择器组件。
  //   输出引脚
endmodule

// MUX
module _2_1MUX (
  input  D0,
  input  D1,
  input  S,
  output Y
);

  wire and_1_out, and_2_out, not_1_out;

  not not_1 (not_1_out, S);
  and and_1 (and_1_out, D0, not_1_out);
  and and_2 (and_2_out, S, D1);
  or or_1 (Y, and_1_out, and_2_out);

  // Notes on the sheet:
  //   输入引脚
  //   请勿修改引脚名称及电路封装外观
  //   提示：使用传输门和晶体管来实现二选一多路选择器，禁止直接使用选择器组件。
  //   输出引脚
endmodule
