// Logisim project lab1.6.circ as structural Verilog: 2 circuits, main circuit 4-1MUX
module _4_1MUX (
  input  [3:0] INPUT,
  input  [1:0] SELECT,
  output OUTPUT
);

  wire n2_1mux_1_y, n2_1mux_2_y;

  _2_1MUX u_2_1mux_1 (.D0(INPUT[0]), .D1(INPUT[1]), .S(SELECT[0]), .Y(n2_1mux_1_y));
  _2_1MUX u_2_1mux_2 (.D0(INPUT[2]), .D1(INPUT[3]), .S(SELECT[0]), .Y(n2_1mux_2_y));
  _2_1MUX u_2_1mux_3 (.D0(n2_1mux_1_y), .D1(n2_1mux_2_y), .S(SELECT[1]), .Y(OUTPUT));

  // Other names for the same wires on the sheet: DATA[3:0] = INPUT; S[1:0] = SELECT; Y = OUTPUT
endmodule

// MUX
module _2_1MUX (
  input  D0,
  input  D1,
  input  S,
  output Y
);

  wire and_1_out, and_2_out, not_1_out;

  not not_1 (not_1_out, S);
  and and_1 (and_1_out, D0, not_1_out);
  and and_2 (and_2_out, S, D1);
  or or_1 (Y, and_1_out, and_2_out);

  // Notes on the sheet:
  //   输入引脚
  //   请勿修改引脚名称及电路封装外观
  //   提示：使用传输门和晶体管来实现二选一多路选择器，禁止直接使用选择器组件。
  //   输出引脚
endmodule
