// Logisim project lab1.7.2.circ as structural Verilog: 1 circuit, main circuit main
module main (
  input  D0,
  input  D1,
  input  D2,
  input  D3,
  output Y0,
  output Y1,
  output Y2,
  output Y3
);

  xor xor_1 (Y0, D0, D1);
  xor xor_2 (Y1, D1, D2);
  xor xor_3 (Y2, D2, D3);

  assign Y3 = D3;

  // Notes on the sheet:
  //   输出引脚
  //   输入引脚（输入值为 (D3D2D1D0)_2）
endmodule
