// Logisim project lab1.7.3.circ as structural Verilog: 1 circuit, main circuit main
module main (
  input  D0,
  input  D1,
  input  D2,
  input  D3,
  output Y0
);

  ExactlyOne xor_1 (.out(Y0), .in0(D0), .in1(D1), .in2(D2), .in3(D3));

  // Notes on the sheet:
  //   输入引脚（输入值为 (D3D2D1D0)_2）
  //   输出引脚（生成的位 Y0 即为奇偶校验位）
endmodule
