// Logisim project lab2.2.circ as structural Verilog: 1 circuit, main circuit main
module main (
  input  I0,
  input  I1,
  input  I2,
  input  I4,
  input  I5,
  input  I3,
  input  I6,
  input  I7,
  output O0,
  output O1,
  output O2
);

  wire _1_out, _2_out, _3_out, _4_out, _5_out, _6_out, _7_out;

  and _1 (_1_out, ~I0, I1);  // AND_Gate
  and _2 (_2_out, ~I0, ~I1, I2);  // AND_Gate
  and _3 (_3_out, ~I0, ~I1, ~I2, I3);  // AND_Gate
  and _4 (_4_out, ~I0, ~I1, ~I2, ~I3, I4);  // AND_Gate
  and _5 (_5_out, ~I0, ~I1, ~I2, ~I3, ~I4, I5);  // AND_Gate
  and _6 (_6_out, ~I0, ~I1, ~I2, ~I3, ~I4, ~I5, I6);  // AND_Gate
  and _7 (_7_out, ~I0, ~I1, ~I2, ~I3, ~I4, ~I5, ~I6, I7);  // AND_Gate
  or or_1 (O0, _4_out, _5_out, _6_out, _7_out);
  or or_2 (O1, _2_out, _3_out, _6_out, _7_out);
  or or_3 (O2, _1_out, _3_out, _5_out, _7_out);
  Hex_Digit_Display hex_digit_display_1 (.value({1'b0, O0, O1, O2}));  // open: dp

  // Notes on the sheet:
  //   输入引脚
  //   请勿修改引脚名称、电路名称及电路封装外观
  //   提示：使用独立逻辑门实现8-3优先级编码器，禁止直接使用编码器组件。
  //   输出引脚
endmodule
