// Logisim project lab2.7.circ as structural Verilog: 2 circuits, main circuit main
module main (
  input  [3:0] X,
  input  [3:0] Y,
  input  OP,
  output [3:0] F,
  output Cout,
  output out_6,
  output CF,
  output OF,
  output SF,
  output ZF,
  output out_11
);

  wire fa_1_cout, fa_2_cout, fa_3_cout, not_1_out, not_2_out, xor_1_out, xor_2_out, xor_3_out, xor_4_out;

  Hex_Digit_Display hex_digit_display_1 (.value(Y), .dp(1'b0));
  xor xor_1 (xor_1_out, 1'b1, X[0]);
  Hex_Digit_Display hex_digit_display_2 (.value(X), .dp(1'b0));
  FA fa_1 (.A(Y[0]), .B(xor_1_out), .Cin(1'b1), .Cout(fa_1_cout), .F(F[0]));
  xor xor_2 (xor_2_out, 1'b1, X[1]);
  Hex_Digit_Display hex_digit_display_3 (.value(F), .dp(1'b0));
  FA fa_2 (.A(Y[1]), .B(xor_2_out), .Cin(fa_1_cout), .Cout(fa_2_cout), .F(F[1]));
  xor xor_3 (xor_3_out, 1'b1, X[2]);
  FA fa_3 (.A(Y[2]), .B(xor_3_out), .Cin(fa_2_cout), .Cout(fa_3_cout), .F(F[2]));
  xor xor_4 (xor_4_out, 1'b1, X[3]);
  FA fa_4 (.A(Y[3]), .B(xor_4_out), .Cin(fa_3_cout), .Cout(Cout), .F(F[3]));
  xor xor_5 (OF, F[3], Cout);
  xor xor_6 (CF, Cout, 1'b1);
  nor nor_1 (ZF, F[3], F[2], F[1], F[0]);
  Multiplexer #(.enable("false")) multiplexer_1 (.in0(CF), .in1(F[3]), .out(out_6), .sel(OP));
  not not_1 (not_1_out, CF);
  Multiplexer #(.enable("false")) multiplexer_2 (.in0(not_1_out), .in1(not_2_out), .out(out_11), .sel(OP));
  not not_2 (not_2_out, F[3]);

  assign SF = F[3];

  // Other names for the same wires on the sheet: SUM[3:0] = F; tunnel = out_11; tunnel_t = out_6; 操作数x[3:0] = X;
  //   操作数y[3:0] = Y

  // Notes on the sheet:
  //   输入引脚
  //   +
  //   提示：使用独立逻辑门及全加器FA子电路实现4位二进制数加减法器，禁止直接使用加减法器组件。
  //   =
  //   请勿修改引脚名称、电路名称及电路封装外观
  //   输出引脚
endmodule

module FA (
  input  A,
  input  B,
  input  Cin,
  output F,
  output Cout
);

  wire and_1_out, and_2_out, and_3_out, xor_1_out;

  xor xor_1 (xor_1_out, A, B);
  and and_1 (and_1_out, A, B);
  and and_2 (and_2_out, B, Cin);
  and and_3 (and_3_out, A, Cin);
  xor xor_2 (F, Cin, xor_1_out);
  or or_1 (Cout, and_1_out, and_2_out, and_3_out);

  // Notes on the sheet:
  //   全加器
endmodule
