// Logisim project lab2.8.circ as structural Verilog: 1 circuit, main circuit main
module main (
  input  [3:0] X,
  input  [3:0] Y,
  output X_Y,
  output X_Y_2,
  output X_Y_3
);

  wire and_1_out, and_2_out, and_3_out, and_4_out, and_5_out, and_6_out, and_7_out, and_8_out, and_9_out,
       and_10_out, and_11_out, and_12_out, and_14_out, and_15_out, and_16_out, and_17_out, xnor_1_out,
       xnor_2_out, xnor_3_out, xnor_4_out;

  xnor xnor_1 (xnor_1_out, X[3], Y[3]);
  and and_1 (and_1_out, X[3], ~Y[3]);  // AND_Gate
  and and_2 (and_2_out, ~X[3], Y[3]);  // AND_Gate
  xnor xnor_2 (xnor_2_out, X[2], Y[2]);
  and and_3 (and_3_out, X[2], ~Y[2]);  // AND_Gate
  and and_4 (and_4_out, ~X[2], Y[2]);  // AND_Gate
  and and_5 (and_5_out, xnor_2_out, xnor_1_out);
  and and_6 (and_6_out, xnor_1_out, and_3_out);
  and and_7 (and_7_out, xnor_1_out, and_4_out);
  xnor xnor_3 (xnor_3_out, X[1], Y[1]);
  and and_8 (and_8_out, X[1], ~Y[1]);  // AND_Gate
  and and_9 (and_9_out, ~X[1], Y[1]);  // AND_Gate
  and and_10 (and_10_out, xnor_3_out, and_5_out);
  and and_11 (and_11_out, and_5_out, and_8_out);
  and and_12 (and_12_out, and_5_out, and_9_out);
  xnor xnor_4 (xnor_4_out, X[0], Y[0]);
  and and_13 (X_Y_2, xnor_4_out, and_10_out);
  and and_14 (and_14_out, and_10_out, and_15_out);
  and and_15 (and_15_out, X[0], ~Y[0]);  // AND_Gate
  and and_16 (and_16_out, and_10_out, and_17_out);
  and and_17 (and_17_out, ~X[0], Y[0]);  // AND_Gate
  or or_1 (X_Y, and_14_out, and_11_out, and_6_out, and_1_out);
  or or_2 (X_Y_3, and_16_out, and_12_out, and_7_out, and_2_out);

  // Other names for the same wires on the sheet: X_Y_t = X_Y_3; X_Y_t_t = X_Y_2; 操作数x[3:0] = X; 操作数y[3:0] = Y

  // Notes on the sheet:
  //   输入引脚
  //   请勿修改引脚名称、电路名称及电路封装外观
  //   输出引脚
endmodule
