// Logisim project lab3.8.circ as structural Verilog: 1 circuit, main circuit main
module main (
  input  [7:0] in_1,
  input  in_2,
  input  in_3
);

  wire xor_1_out, xor_2_out, xor_3_out;

  SHRG4U shrg4u_1 (
    .CLK(in_2), .CLR_L(1'b1), .RIN(xor_3_out), .Q3(in_1[7]), .Q2(in_1[6]), .D3(1'b0), .D2(1'b0), .D1(1'b0),
    .Q1(in_1[5]), .Q0(in_1[4]), .D0(1'b0), .LIN(1'b1), .S1(1'b1), .S0(in_3));
  SHRG4U shrg4u_2 (
    .CLK(in_2), .CLR_L(1'b1), .RIN(in_1[4]), .Q3(in_1[3]), .Q2(in_1[2]), .D3(1'b0), .D2(1'b0), .D1(1'b0),
    .Q1(in_1[1]), .Q0(in_1[0]), .D0(1'b1), .LIN(1'b1), .S1(1'b1), .S0(in_3));
  Hex_Digit_Display hex_digit_display_1 (.value(in_1[7:4]));  // open: dp
  xor xor_1 (xor_1_out, in_1[4], in_1[3]);
  Hex_Digit_Display hex_digit_display_2 (.value(in_1[3:0]));  // open: dp
  xor xor_2 (xor_2_out, xor_1_out, in_1[2]);
  xor xor_3 (xor_3_out, xor_2_out, in_1[0]);
endmodule
