// Logisim project lab4.6.circ as structural Verilog: 1 circuit, main circuit main
module main (
  input  [31:0] X1,
  input  [31:0] X0,
  input  [31:0] Y1,
  input  [31:0] Y0,
  input  Cin,
  output out_6,
  output [31:0] Z1,
  output out_8,
  output out_9,
  output [31:0] Z0
);

  wire adder16_1_gg, adder16_1_pg, adder16_2_pg, adder16_3_gg, adder16_3_pg, adder16_4_pg, clu4_1_c1,
       clu4_1_c2, clu4_1_c3;

  Adder16 adder16_1 (
    .X(X1[31:16]), .Y(Y1[31:16]), .C0(clu4_1_c3), .S(Z1[31:16]), .C16(out_9), .Pg(adder16_1_pg),
    .Gg(adder16_1_gg));
  Adder16 adder16_2 (
    .X(X1[15:0]), .Y(Y1[15:0]), .C0(clu4_1_c2), .S(Z1[15:0]), .Pg(adder16_2_pg), .Gg(adder16_2_pg));  // open: C16
  CLU4 clu4_1 (
    .P0(adder16_4_pg), .P1(adder16_3_pg), .P2(adder16_2_pg), .P3(adder16_1_pg), .C1(clu4_1_c1),
    .C3(clu4_1_c3), .G0(adder16_4_pg), .G1(adder16_3_gg), .G2(adder16_2_pg), .G3(adder16_1_gg),
    .C2(clu4_1_c2), .C0(Cin), .Pg(out_6), .Gg(out_8));  // open: C4
  Adder16 adder16_3 (
    .X(X0[31:16]), .Y(Y0[31:16]), .C0(clu4_1_c1), .S(Z0[31:16]), .Pg(adder16_3_pg), .Gg(adder16_3_gg));  // open: C16
  Adder16 adder16_4 (
    .X(X0[15:0]), .Y(Y0[15:0]), .C0(Cin), .S(Z0[15:0]), .Pg(adder16_4_pg), .Gg(adder16_4_pg));  // open: C16

  // Other names for the same wires on the sheet: C64 = out_9; Gg = out_8; Pg = out_6
endmodule
