// Logisim project lab4.7.circ as structural Verilog: 4 circuits, main circuit main
module main (
  input  CLK,
  input  [31:0] X,
  input  [31:0] Y,
  input  Reset,
  output [31:0] Prod0,
  output [31:0] Prod1
);

  wire LOAD, not_1_out, STOP;
  wire [5:0] counter_1_q;
  wire [31:0] adder32_1_s, multiplexer_1_out, multiplexer_2_out;
  wire [31:31] adder32_1_cout;

  not not_1 (not_1_out, STOP);
  Multiplexer #(.width(32), .enable("false")) multiplexer_1 (
    .in0({32{1'b0}}), .in1(X), .out(multiplexer_1_out), .sel(Prod0[0]));
  Adder32 adder32_1 (
    .Cin(1'b0), .Cout(adder32_1_cout[31]), .X(Prod1), .Y(multiplexer_1_out), .S(adder32_1_s));  // open: OF, CF, ZF, SF
  Register #(.width(32), .trigger("falling"), .Select("low")) register_1 (
    .D({adder32_1_cout[31], adder32_1_s[31:1]}), .en(not_1_out), .Q(Prod1), .clk(CLK), .clr(Reset));
  // Probe on X
  // Probe on Y
  // Probe on Prod1
  Register #(.width(32), .trigger("falling"), .Select("low")) u_Y (
    .D(multiplexer_2_out), .en(not_1_out), .Q(Prod0), .clk(CLK), .clr(Reset));
  Multiplexer #(.width(32), .enable("false")) multiplexer_2 (
    .in0({adder32_1_s[0], Prod0[31:1]}), .in1(Y), .out(multiplexer_2_out), .sel(LOAD));
  Counter #(.width(6), .max('h3f), .trigger("falling")) counter_1 (
    .load(1'b0), .count(not_1_out), .Q(counter_1_q), .clk(CLK), .clr(Reset), .preset(1'b0), .down(1'b0));  // open: D, carry
  // Probe on Prod0
  Comparator #(.width(6), .mode("unsigned")) comparator_1 (.a(counter_1_q), .b({6{1'b0}}), .eq(LOAD));  // open: gt, lt
  Comparator #(.width(6), .mode("unsigned")) comparator_2 (.a(counter_1_q), .b(6'b100001), .eq(STOP));  // open: gt, lt

  // Other names for the same wires on the sheet: RST = Reset; Z0[31:0] = Prod0; Z1[31:0] = Prod1

  // Notes on the sheet:
  //   ×
  //   =
  //   P
endmodule

module ADDER4b (
  input  [3:0] X,
  input  [3:0] Y,
  input  Cin,
  output [3:0] F,
  output Cout
);

  wire fa_1_cout, fa_2_cout, fa_3_cout;
  wire [3:0] bit_extender_1_out, xor_1_out;

  assign bit_extender_1_out = {{3{Cin}}, Cin};  // Bit_Extender bit_extender_1
  Hex_Digit_Display hex_digit_display_1 (.value(X), .dp(1'b0));
  assign xor_1_out = bit_extender_1_out ^ Y;  // XOR_Gate xor_1, 4 bits wide
  Hex_Digit_Display hex_digit_display_2 (.value(xor_1_out), .dp(1'b0));
  FA fa_1 (.A(X[0]), .B(xor_1_out[0]), .Cin(Cin), .F(F[0]), .Cout(fa_1_cout));
  Hex_Digit_Display hex_digit_display_3 (.value(F), .dp(1'b0));
  FA fa_2 (.A(X[1]), .B(xor_1_out[1]), .Cin(fa_1_cout), .F(F[1]), .Cout(fa_2_cout));
  FA fa_3 (.A(X[2]), .B(xor_1_out[2]), .Cin(fa_2_cout), .F(F[2]), .Cout(fa_3_cout));
  FA fa_4 (.A(X[3]), .B(xor_1_out[3]), .Cin(fa_3_cout), .F(F[3]), .Cout(Cout));

  // Other names for the same wires on the sheet: SUM[3:0] = F; 操作数x[3:0] = X; 操作数y[3:0] = Y

  // Notes on the sheet:
  //   输入引脚
  //   +
  //   =
  //   请勿修改引脚名称、电路名称及电路封装外观
  //   提示：使用独立逻辑门及全加器FA子电路实现4位二进制数加减法器，禁止直接使用加减法器组件。
  //   输出引脚
endmodule

module FA (
  input  A,
  input  B,
  input  Cin,
  output F,
  output Cout
);

  wire and_1_out, and_2_out, and_3_out;

  xor xor_1 (F, A, B, Cin);
  and and_1 (and_1_out, A, B);
  and and_2 (and_2_out, B, Cin);
  and and_3 (and_3_out, A, Cin);
  or or_1 (Cout, and_1_out, and_2_out, and_3_out);

  // Notes on the sheet:
  //   全加器
endmodule

module BarrelSFT8b (
  input  [7:0] DataIn,
  input  [2:0] shamt,
  input  IN,
  input  L_R,
  input  A_L,
  output [7:0] DataOut
);

  wire [0:0] multiplexer_1_out;
  wire [1:0] multiplexer_4_out;
  wire [3:0] multiplexer_6_out;
  wire [7:0] multiplexer_3_out, multiplexer_5_out;
  wire [7:7] multiplexer_2_out;

  Multiplexer #(.enable("false")) multiplexer_1 (.in0(IN), .in1(DataIn[7]), .out(multiplexer_1_out[0]), .sel(A_L));
  Multiplexer #(.enable("false")) multiplexer_2 (.in0(IN), .in1(DataIn[7]), .out(multiplexer_2_out[7]), .sel(A_L));
  Multiplexer #(.select(2), .width(8), .enable("false")) multiplexer_3 (
    .in0(DataIn), .in1({multiplexer_2_out[7], DataIn[7:1]}), .in2(DataIn),
    .in3({DataIn[6:0], multiplexer_1_out[0]}), .out(multiplexer_3_out), .sel({L_R, shamt[0]}));
  Multiplexer #(.width(2), .enable("false")) multiplexer_4 (
    .in0({2{IN}}), .in1(multiplexer_3_out[7:6]), .out(multiplexer_4_out), .sel(A_L));
  Multiplexer #(.select(2), .width(8), .enable("false")) multiplexer_5 (
    .in0(multiplexer_3_out), .in1({{2{multiplexer_1_out[0]}}, multiplexer_3_out[7:2]}),
    .in2(multiplexer_3_out), .in3({multiplexer_3_out[5:0], multiplexer_4_out}), .out(multiplexer_5_out),
    .sel({L_R, shamt[1]}));
  Multiplexer #(.width(4), .enable("false")) multiplexer_6 (
    .in0({4{IN}}), .in1(multiplexer_5_out[7:4]), .out(multiplexer_6_out), .sel(A_L));
  Multiplexer #(.select(2), .width(8), .enable("false")) multiplexer_7 (
    .in0(multiplexer_5_out), .in1({{4{multiplexer_1_out[0]}}, multiplexer_5_out[7:4]}),
    .in2(multiplexer_5_out), .in3({multiplexer_5_out[3:0], multiplexer_6_out}), .out(DataOut),
    .sel({L_R, shamt[2]}));

  // Other names for the same wires on the sheet: Din[7:0] = DataIn; Input = IN; Left_Right = L_R; Arth_Logic = A_L;
  //   Dout[7:0] = DataOut

  // Notes on the sheet:
  //   L/R,A/L: 00逻辑右移，01算术右移，10逻辑左移，11：循环左移
  //   输入引脚
  //   请勿修改引脚名称、电路名称及电路封装外观
  //   提示：使用多路选择器级联实现8位桶形移位器，禁止直接使用移位器组件。
  //   输出引脚
endmodule
