// Logisim project lab5.2.circ as structural Verilog: 1 circuit, main circuit DataRam
// DataRAM
module DataRam (
  input  CLK,
  input  CLR,
  input  WE,
  input  [2:0] MemOp,
  input  [17:0] Addr,
  input  [31:0] Din,
  output AlignErr,
  output [31:0] DataOut
);

  wire and_1_out, and_2_out, and_3_out, and_4_out, and_5_out, and_6_out, and_7_out, and_8_out, and_9_out,
       and_10_out, and_11_out, and_12_out, and_13_out, and_14_out, not_1_out;
  wire [3:0] SEL;
  wire [7:0] IN0, IN1, IN2, IN3, OUT0, OUT1, OUT2, OUT3;
  wire [31:0] bit_extender_1_out, bit_extender_2_out, bit_extender_3_out, bit_extender_4_out,
       bit_extender_5_out, bit_extender_6_out, bit_extender_7_out, bit_extender_8_out, bit_extender_9_out,
       bit_extender_10_out, bit_extender_11_out, bit_extender_12_out, multiplexer_1_out, multiplexer_2_out,
       multiplexer_3_out, multiplexer_4_out, multiplexer_5_out, multiplexer_6_out;

  and and_1 (and_1_out, ~Addr[0], ~Addr[1]);  // AND_Gate
  and and_2 (and_2_out, Addr[0], ~Addr[1]);  // AND_Gate
  and and_3 (and_3_out, ~Addr[0], Addr[1]);  // AND_Gate
  and and_4 (and_4_out, Addr[0], Addr[1]);
  and and_5 (and_5_out, ~MemOp[0], ~MemOp[1], ~MemOp[2]);  // AND_Gate
  and and_6 (and_6_out, MemOp[0], ~MemOp[1]);  // AND_Gate
  and and_7 (and_7_out, ~MemOp[0], MemOp[1]);  // AND_Gate
  not not_1 (not_1_out, MemOp[2]);
  assign bit_extender_1_out = {{24{1'b0}}, OUT0};  // Bit_Extender bit_extender_1
  assign bit_extender_2_out = {{24{1'b0}}, OUT1};  // Bit_Extender bit_extender_2
  assign bit_extender_3_out = {{24{1'b0}}, OUT2};  // Bit_Extender bit_extender_3
  assign bit_extender_4_out = {{24{1'b0}}, OUT3};  // Bit_Extender bit_extender_4
  assign bit_extender_5_out = {{16{1'b0}}, {OUT1, OUT0}};  // Bit_Extender bit_extender_5
  assign bit_extender_6_out = {{16{1'b0}}, {OUT3, OUT2}};  // Bit_Extender bit_extender_6
  RAM #(.addrWidth(16), .bus("separate"), .Select("high"), .simpleMode("false")) ram_1 (
    .addr(Addr[17:2]), .din(IN3), .data(OUT3), .str(WE), .sel(SEL[3]), .clk(CLK), .clr(CLR));  // open: ld
  and and_8 (and_8_out, and_5_out, and_1_out);
  and and_9 (and_9_out, and_6_out, and_1_out);
  and and_10 (and_10_out, and_6_out, and_2_out);
  and and_11 (and_11_out, and_6_out, and_3_out);
  and and_12 (and_12_out, and_6_out, and_4_out);
  and and_13 (and_13_out, and_7_out, and_1_out);
  and and_14 (and_14_out, and_7_out, and_3_out);
  assign bit_extender_7_out = {{24{OUT0[7]}}, OUT0};  // Bit_Extender bit_extender_7
  assign bit_extender_8_out = {{24{OUT1[7]}}, OUT1};  // Bit_Extender bit_extender_8
  assign bit_extender_9_out = {{24{OUT2[7]}}, OUT2};  // Bit_Extender bit_extender_9
  assign bit_extender_10_out = {{24{OUT3[7]}}, OUT3};  // Bit_Extender bit_extender_10
  assign bit_extender_11_out = {{16{OUT1[7]}}, {OUT1, OUT0}};  // Bit_Extender bit_extender_11
  assign bit_extender_12_out = {{16{OUT3[7]}}, {OUT3, OUT2}};  // Bit_Extender bit_extender_12
  Multiplexer #(.width(32), .enable("false")) multiplexer_1 (
    .in0(bit_extender_7_out), .in1(bit_extender_1_out), .out(multiplexer_1_out), .sel(not_1_out));
  Multiplexer #(.width(32), .enable("false")) multiplexer_2 (
    .in0(bit_extender_8_out), .in1(bit_extender_2_out), .out(multiplexer_2_out), .sel(not_1_out));
  Multiplexer #(.width(32), .enable("false")) multiplexer_3 (
    .in0(bit_extender_9_out), .in1(bit_extender_3_out), .out(multiplexer_3_out), .sel(not_1_out));
  Multiplexer #(.width(32), .enable("false")) multiplexer_4 (
    .in0(bit_extender_10_out), .in1(bit_extender_4_out), .out(multiplexer_4_out), .sel(not_1_out));
  Multiplexer #(.width(32), .enable("false")) multiplexer_5 (
    .in0(bit_extender_11_out), .in1(bit_extender_5_out), .out(multiplexer_5_out), .sel(not_1_out));
  Multiplexer #(.width(32), .enable("false")) multiplexer_6 (
    .in0(bit_extender_12_out), .in1(bit_extender_6_out), .out(multiplexer_6_out), .sel(not_1_out));
  or or_1 (SEL[0], and_8_out, and_13_out, and_9_out);
  or or_2 (SEL[1], and_8_out, and_13_out, and_10_out);
  or or_3 (SEL[2], and_8_out, and_14_out, and_11_out);
  or or_4 (SEL[3], and_8_out, and_14_out, and_12_out);
  nor nor_1 (AlignErr, and_8_out, and_14_out, and_9_out, and_10_out, and_11_out, and_12_out, and_13_out);
  Multiplexer #(.select(4), .width(32), .enable("false")) multiplexer_7 (
    .in1(multiplexer_1_out), .in2(multiplexer_2_out), .in3(multiplexer_5_out), .in4(multiplexer_3_out),
    .in8(multiplexer_4_out), .in12(multiplexer_6_out), .in15({OUT3, OUT2, OUT1, OUT0}), .out(DataOut),
    .sel(SEL));  // open: in0, in5, in6, in7, in9, in10, in11, in13, in14
  RAM #(.addrWidth(16), .bus("separate"), .Select("high"), .simpleMode("false")) ram_2 (
    .addr(Addr[17:2]), .din(IN2), .data(OUT2), .str(WE), .sel(SEL[2]), .clk(CLK), .clr(CLR));  // open: ld
  RAM #(.addrWidth(16), .bus("separate"), .Select("high"), .simpleMode("false")) ram_3 (
    .addr(Addr[17:2]), .din(IN1), .data(OUT1), .str(WE), .sel(SEL[1]), .clk(CLK), .clr(CLR));  // open: ld
  Multiplexer #(.select(4), .width(8), .enable("false")) multiplexer_8 (
    .in1(Din[7:0]), .in3(Din[7:0]), .in15(Din[7:0]), .out(IN0), .sel(SEL));  // open: in0, in2, in4, in5, in6, in7, in8, in9, in10, in11, in12, in13, in14
  Multiplexer #(.select(4), .width(8), .enable("false")) multiplexer_9 (
    .in2(Din[7:0]), .in3(Din[15:8]), .in15(Din[15:8]), .out(IN1), .sel(SEL));  // open: in0, in1, in4, in5, in6, in7, in8, in9, in10, in11, in12, in13, in14
  Multiplexer #(.select(4), .width(8), .enable("false")) multiplexer_10 (
    .in4(Din[7:0]), .in12(Din[7:0]), .in15(Din[23:16]), .out(IN2), .sel(SEL));  // open: in0, in1, in2, in3, in5, in6, in7, in8, in9, in10, in11, in13, in14
  Multiplexer #(.select(4), .width(8), .enable("false")) multiplexer_11 (
    .in8(Din[7:0]), .in12(Din[15:8]), .in15(Din[31:24]), .out(IN3), .sel(SEL));  // open: in0, in1, in2, in3, in4, in5, in6, in7, in9, in10, in11, in13, in14
  RAM #(.addrWidth(16), .bus("separate"), .Select("high"), .simpleMode("false")) ram_4 (
    .addr(Addr[17:2]), .din(IN0), .data(OUT0), .str(WE), .sel(SEL[0]), .clk(CLK), .clr(CLR));  // open: ld

  // Other names for the same wires on the sheet: Dout[31:0] = DataOut

  // Notes on the sheet:
  //   输入引脚
  //   请勿修改引脚名称、电路名称及电路封装外观
  //   为了后续实验中的引用，不要修改MemOp的编码定义、引脚名称和在布局中的位置。
  //   32位数据存储器，按字节分4片存储，可按照字节、半字和字进行存储；读取字节或半字时，支持0扩展和符号位扩展。
  //   输出引脚
endmodule
