// Logisim project lab6.1.circ as structural Verilog: 1 circuit, main circuit 控制器
module \控制器  (
  input  [6:0] opcode,
  input  [2:0] funct3,
  input  [6:0] funct7,
  output [2:0] ExtOp,
  output RegWr,
  output [2:0] BandJ,
  output ALUASrc,
  output [1:0] ALUBSrc,
  output [3:0] ALUctr,
  output MemtoReg,
  output [2:0] MemOp,
  output MemWr
);

  wire and_1_out, B_beq___B_bgeu, comparator_11_eq, Halt, I_addi___I_srai, J_jalr, or_1_out, or_8_out,
       or_9_out, or_12_out, R_add___R_and, U_auipc, U_lui;
  wire [1:0] or_11_out;
  wire [2:0] multiplexer_5_out, multiplexer_6_out;
  wire [3:0] multiplexer_2_out, multiplexer_3_out;
  wire [3:3] multiplexer_1_out;

  Comparator #(.width(7)) comparator_1 (.a(opcode), .b(7'b0110111), .eq(U_lui));  // open: gt, lt
  Comparator #(.width(7)) comparator_2 (.a(opcode), .b(7'b0010111), .eq(U_auipc));  // open: gt, lt
  Comparator #(.width(7)) comparator_3 (.a(opcode), .b(7'b0010011), .eq(I_addi___I_srai));  // open: gt, lt
  Comparator #(.width(7)) comparator_4 (.a(opcode), .b(7'b0110011), .eq(R_add___R_and));  // open: gt, lt
  Comparator #(.width(7)) comparator_5 (.a(opcode), .b(7'b1101111), .eq(ExtOp[2]));  // open: gt, lt
  Comparator #(.width(7)) comparator_6 (.a(opcode), .b(7'b1100111), .eq(J_jalr));  // open: gt, lt
  Comparator #(.width(7)) comparator_7 (.a(opcode), .b(7'b1100011), .eq(B_beq___B_bgeu));  // open: gt, lt
  Comparator #(.width(7)) comparator_8 (.a(opcode), .b(7'b0000011), .eq(MemtoReg));  // open: gt, lt
  Comparator #(.width(7)) comparator_9 (.a(opcode), .b(7'b0100011), .eq(MemWr));  // open: gt, lt
  Comparator #(.width(7)) comparator_10 (.a(opcode), .b(7'b1110011), .eq(Halt));  // open: gt, lt
  and and_1 (and_1_out, I_addi___I_srai, comparator_11_eq);
  Comparator #(.width(3), .mode("unsigned")) comparator_11 (
    .a(funct3), .b(3'b101), .eq(comparator_11_eq));  // open: gt, lt
  Multiplexer #(.enable("false")) multiplexer_1 (
    .in0(1'b0), .in1(funct7[5]), .out(multiplexer_1_out[3]), .sel(or_1_out));
  or or_1 (or_1_out, and_1_out, R_add___R_and);
  or or_2 (ExtOp[0], U_lui, U_auipc, B_beq___B_bgeu);
  or or_3 (ExtOp[1], B_beq___B_bgeu, MemWr);
  or or_4 (ALUASrc, ExtOp[2], J_jalr, U_auipc);
  or or_5 (ALUBSrc[0], ExtOp[2], J_jalr);
  or or_6 (RegWr, U_lui, U_auipc, J_jalr, R_add___R_and, ExtOp[2], I_addi___I_srai, MemtoReg);
  or or_7 (ALUBSrc[1], MemtoReg, U_lui, I_addi___I_srai, MemWr, U_auipc);
  Multiplexer #(.width(4), .enable("false")) multiplexer_2 (
    .in0(4'b0000), .in1(4'b1111), .out(multiplexer_2_out), .sel(U_lui));
  Multiplexer #(.width(4), .enable("false")) multiplexer_3 (
    .in0({3'b001, funct3[1]}), .in1({multiplexer_1_out[3], funct3}), .out(multiplexer_3_out), .sel(or_8_out));
  or or_8 (or_8_out, I_addi___I_srai, R_add___R_and);
  Multiplexer #(.width(4), .enable("false")) multiplexer_4 (
    .in0(multiplexer_2_out), .in1(multiplexer_3_out), .out(ALUctr), .sel(or_9_out));
  or or_9 (or_9_out, or_8_out, B_beq___B_bgeu);
  or or_10 (or_11_out[1], ExtOp[2], J_jalr);
  Multiplexer #(.select(3), .width(3), .enable("false")) multiplexer_5 (
    .in0(3'b100), .in1(3'b101), .in4(3'b110), .in5(3'b111), .in6(3'b110), .in7(3'b111),
    .out(multiplexer_5_out), .sel(funct3));  // open: in2, in3
  or or_11 (or_11_out[0], J_jalr, B_beq___B_bgeu);
  Multiplexer #(.select(3), .width(3), .enable("false")) multiplexer_6 (
    .in0(3'b101), .in1(3'b110), .in2(3'b000), .in3(3'b000), .in4(3'b001), .in5(3'b010),
    .out(multiplexer_6_out), .sel(funct3));  // open: in6, in7
  or or_12 (or_12_out, MemWr, MemtoReg);
  Multiplexer #(.select(2), .width(3), .enable("false")) multiplexer_7 (
    .in0(3'b000), .in1(multiplexer_5_out), .in2(3'b001), .in3(3'b010), .out(BandJ), .sel(or_11_out));
  Multiplexer #(.width(3), .enable("false")) multiplexer_8 (
    .in0(3'b000), .in1(multiplexer_6_out), .out(MemOp), .sel(or_12_out));

  // Other names for the same wires on the sheet: J_jal = ExtOp[2]; I_lb___I_lhu = MemtoReg; S_sb___S_sw = MemWr

  // Notes on the sheet:
  //   输入引脚
  //   请勿修改引脚名称、电路名称及电路封装外观
  //   提示：根据指令种类，把7位指令code用一位指令类型标志位来表示，再通过功能码来区分具体指令，生成控制信号。
  //   输出引脚
endmodule
