// Logisim project lab6.5.circ as structural Verilog: 16 circuits, main circuit main
module main (
  input  ReSet,
  input  [31:0] Init_Addr,
  input  clk,
  output [31:0] PC,
  output [31:0] IR,
  output [31:0] BusW,
  output [31:0] Din,
  output [15:0] Cycles,
  output Halt
);

  wire alu_1_zero, clk_out, clk_t, not_2_out, NPCASrc, NPCBSrc, \控制器_1_aluasrc , \控制器_1_memtoreg ,
       \控制器_1_memwr , \控制器_1_regwr ;
  wire [1:0] \控制器_1_alubsrc ;
  wire [2:0] idu_1_funct3, \控制器_1_bandj , \控制器_1_extop , \控制器_1_memop ;
  wire [3:0] \控制器_1_aluctr ;
  wire [6:0] idu_1_funct7, idu_1_opcode;
  wire [31:0] alu_1_s, dataram_1_dataout, idu_1_busa, idu_1_dataa, idu_1_datab, idu_1_imm;

  \控制器  \u_控制器_1  (
    .opcode(idu_1_opcode), .ExtOp(\控制器_1_extop ), .RegWr(\控制器_1_regwr ), .BandJ(\控制器_1_bandj ),
    .funct3(idu_1_funct3), .ALUASrc(\控制器_1_aluasrc ), .ALUBSrc(\控制器_1_alubsrc ), .ALUctr(\控制器_1_aluctr ),
    .funct7(idu_1_funct7), .MemtoReg(\控制器_1_memtoreg ), .MemOp(\控制器_1_memop ), .MemWr(\控制器_1_memwr ),
    .Halt(Halt));
  Clock u_clk (.out(clk_out));
  not not_1 (clk_t, clk_out);
  IFU ifu_1 (
    .CLK(clk_t), .Reset(ReSet), .NPCASrc(NPCASrc), .NPCBSrc(NPCBSrc), .Initial_Address(Init_Addr),
    .Imm(idu_1_imm), .BusA(idu_1_busa), .PC(PC), .halt(Halt));
  IDU idu_1 (
    .IR(IR), .BusW(BusW), .PC(PC), .DataA(idu_1_dataa), .DataB(idu_1_datab), .BusA(idu_1_busa), .BusB(Din),
    .OpCode(idu_1_opcode), .ExtOp(\控制器_1_extop ), .RegWr(\控制器_1_regwr ), .Imm(idu_1_imm),
    .Funct3(idu_1_funct3), .ALUASrc(\控制器_1_aluasrc ), .ALUBSrc(\控制器_1_alubsrc ), .Funct7(idu_1_funct7),
    .CLK(clk_t));
  ALU alu_1 (.A(idu_1_dataa), .B(idu_1_datab), .ALUctr(\控制器_1_aluctr ), .S(alu_1_s), .Zero(alu_1_zero));
  ROM #(.addrWidth(16), .dataWidth(32), .Select("high")) rom_1 (.addr(PC[17:2]), .data(IR));
  BandJ bandj_1 (.BandJ(\控制器_1_bandj ), .NPCASrc(NPCASrc), .Zero(alu_1_zero), .NPCBSrc(NPCBSrc), .Result0(alu_1_s[0]));
  Multiplexer #(.width(32), .enable("false")) multiplexer_1 (
    .in0(alu_1_s), .in1(dataram_1_dataout), .out(BusW), .sel(\控制器_1_memtoreg ));
  DataRAM dataram_1 (
    .CLK(clk_t), .CLR(ReSet), .WE(\控制器_1_memwr ), .MemOp(\控制器_1_memop ), .Addr(alu_1_s[17:0]), .Din(Din),
    .DataOut(dataram_1_dataout));  // open: AlignErr
  // Probe on Cycles
  Counter #(.width(16), .max('hffff), .behavior("old")) \u_计数器  (
    .count(not_2_out), .Q(Cycles), .clk(clk_t), .clr(ReSet));  // open: load, D, carry, preset
  not not_2 (not_2_out, Halt);

  // Notes on the sheet:
  //   输入引脚
  //   请勿修改引脚名称、电路名称及电路封装外观
  //   指令存储器和数据存储器数据位都是32位，指令存储器编址以字为单位，数据存储器编址以字节为单位。
  //   引用取指令部件、取操作数部件、ALU部件、数据存储器、分支控制器、指令存储器等部件，完成单周期CPU设计。
  //   输出引脚
  //   状态元件的触发条件都设置成上升沿触发，时钟输入信号通过反相器输入。
  //   contents of rom_1 (hex, n*v repeats v):
  //   93 113 193 213 293 313 393 413 493 513 593 613 693 713 793 813 893 913 993 a13 a93 b13 b93 c13 c93
  //   d13 d93 e13 e93 f13 f93 93 113 208733 393 200193 4c771663 100093 100113 208733 200393 300193
  //   4a771a63 300093 700113 208733 a00393 400193 48771e63 93 ffff8137 208733 ffff83b7 500193 48771263
  //   800000b7 113 208733 800003b7 600193 46771663 800000b7 ffff8137 208733 7fff83b7 700193 44771a63 93
  //   8137 fff10113 208733 83b7 fff38393 800193 42771a63 800000b7 fff08093 113 208733 800003b7 fff38393
  //   900193 40771a63 800000b7 fff08093 8137 fff10113 208733 800083b7 ffe38393 a00193 3e771863 800000b7
  //   8137 fff10113 208733 800083b7 fff38393 b00193 3c771863 800000b7 fff08093 ffff8137 208733 7fff83b7
  //   fff38393 c00193 3a771863 93 fff00113 208733 fff00393 d00193 38771c63 fff00093 100113 208733 393
  //   e00193 38771063 fff00093 fff00113 208733 ffe00393 f00193 36771463 100093 80000137 fff10113 208733
  //   800003b7 1000193 34771663 d00093 b00113 2080b3 1800393 1100193 32709a63 e00093 b00113 208133 1900393
  //   1200193 30711e63 d00093 1080b3 1a00393 1300193 30709463 213 d00093 b00113 208733 70313 120213 200293
  //   fe5214e3 1800393 1400193 2c731e63 213 e00093 b00113 208733 13 70313 120213 200293 fe5212e3 1900393
  //   1500193 2a731663 213 f00093 b00113 208733 13 13 70313 120213 200293 fe5210e3 1a00393 1600193
  //   26731c63 213 d00093 b00113 208733 120213 200293 fe5216e3 1800393 1700193 24771863 213 e00093 b00113
  //   13 208733 120213 200293 fe5214e3 1900393 1800193 22771263 213 f00093 b00113 13 13 208733 120213
  //   200293 fe5212e3 1a00393 1900193 1e771a63 213 d00093 13 b00113 208733 120213 200293 fe5214e3 1800393
  //   1a00193 1c771463 213 e00093 13 b00113 13 208733 120213 200293 fe5212e3 1900393 1b00193 18771c63 213
  //   f00093 13 13 b00113 208733 120213 200293 fe5212e3 1a00393 1c00193 16771463 213 b00113 d00093 208733
  //   120213 200293 fe5216e3 1800393 1d00193 14771063 213 b00113 e00093 13 208733 120213 200293 fe5214e3
  //   1900393 1e00193 10771a63 213 b00113 f00093 13 13 208733 120213 200293 fe5212e3 1a00393 1f00193
  //   e771263 213 b00113 13 d00093 208733 120213 200293 fe5214e3 1800393 2000193 a771c63 213 b00113 13
  //   e00093 13 208733 120213 200293 fe5212e3 1900393 2100193 8771463 213 b00113 13 13 f00093 208733
  //   120213 200293 fe5212e3 1a00393 2200193 4771c63 f00093 100133 f00393 2300193 4711263 2000093 8133
  //   2000393 2400193 2711863 b3 393 2500193 2709063 1000093 1e00113 208033 393 2600193 701463 301863
  //   deade537 ead50513 dead10cc c10537 fee50513 dead10cc c0001073
  //   程序执行周期数
endmodule

module BandJ (
  input  [2:0] BandJ,
  input  Zero,
  input  Result0,
  output NPCASrc,
  output NPCBSrc
);

  wire not_1_out, or_1_out;

  Multiplexer #(.select(3), .enable("false")) multiplexer_1 (
    .in0(1'b0), .in1(1'b0), .in2(1'b1), .in4(1'b0), .in5(1'b0), .in6(1'b0), .in7(1'b0), .out(NPCASrc),
    .sel(BandJ));  // open: in3
  or or_1 (or_1_out, ~Result0, Zero);  // OR_Gate
  Multiplexer #(.select(3), .enable("false")) multiplexer_2 (
    .in0(1'b0), .in1(1'b1), .in2(1'b1), .in4(Zero), .in5(not_1_out), .in6(Result0), .in7(or_1_out),
    .out(NPCBSrc), .sel(BandJ));  // open: in3
  not not_1 (not_1_out, Zero);

  // Notes on the sheet:
  //   BandJ: pull=down
  //   Zero: pull=down
  //   输入信号
  //   请勿修改引脚名称、电路名称及电路封装外观
  //   不要修改控制信号的编码定义、引脚名称和在布局中的位置。
  //   输出信号
endmodule

module IFU (
  input  [31:0] Initial_Address,
  input  [31:0] Imm,
  input  [31:0] BusA,
  input  CLK,
  input  Reset,
  input  halt,
  input  NPCASrc,
  input  NPCBSrc,
  output [31:0] PC
);

  wire not_1_out;
  wire [31:0] adder_1_out, multiplexer_1_out, multiplexer_2_out, multiplexer_3_out;

  Multiplexer #(.width(32), .enable("false")) multiplexer_1 (
    .in0(PC), .in1(BusA), .out(multiplexer_1_out), .sel(NPCASrc));
  Multiplexer #(.width(32), .enable("false")) multiplexer_2 (
    .in0(32'h4), .in1(Imm), .out(multiplexer_2_out), .sel(NPCBSrc));
  Adder #(.width(32)) adder_1 (.a(multiplexer_1_out), .b(multiplexer_2_out), .out(adder_1_out));  // open: cin, cout
  Multiplexer #(.width(32), .enable("false")) multiplexer_3 (
    .in0(adder_1_out), .in1(Initial_Address), .out(multiplexer_3_out), .sel(Reset));
  not not_1 (not_1_out, halt);
  Register #(.width(32), .Select("low")) register_1 (
    .D(multiplexer_3_out), .en(not_1_out), .Q(PC), .clk(CLK), .clr(Reset));

  // Other names for the same wires on the sheet: Init_Addr[31:0] = Initial_Address

  // Notes on the sheet:
  //   NPCBSrc: pull=down
  //   NPCASrc: pull=down
  //   BusA: pull=down
  //   Imm: pull=down
  //   请勿修改引脚名称、电路名称及电路封装外观
  //   指令存储器256KB，数据位为32位，地址位为16位。PC寄存器数据宽度32位，片选信号高电平有效
  //   输入信号
  //   输出信号
endmodule

module \控制器  (
  input  [6:0] opcode,
  input  [2:0] funct3,
  input  [6:0] funct7,
  output [2:0] ExtOp,
  output RegWr,
  output [2:0] BandJ,
  output ALUASrc,
  output [1:0] ALUBSrc,
  output [3:0] ALUctr,
  output MemtoReg,
  output [2:0] MemOp,
  output MemWr,
  output Halt
);

  wire and_1_out, B_beq___B_bgeu, comparator_11_eq, I_addi___I_srai, J_jalr, or_1_out, or_8_out, or_9_out,
       or_12_out, R_add___R_and, U_auipc, U_lui;
  wire [1:0] or_11_out;
  wire [2:0] multiplexer_5_out, multiplexer_6_out;
  wire [3:0] multiplexer_2_out, multiplexer_3_out;
  wire [3:3] multiplexer_1_out;

  Comparator #(.width(7)) comparator_1 (.a(opcode), .b(7'b0110111), .eq(U_lui));  // open: gt, lt
  Comparator #(.width(7)) comparator_2 (.a(opcode), .b(7'b0010111), .eq(U_auipc));  // open: gt, lt
  Comparator #(.width(7)) comparator_3 (.a(opcode), .b(7'b0010011), .eq(I_addi___I_srai));  // open: gt, lt
  Comparator #(.width(7)) comparator_4 (.a(opcode), .b(7'b0110011), .eq(R_add___R_and));  // open: gt, lt
  Comparator #(.width(7)) comparator_5 (.a(opcode), .b(7'b1101111), .eq(ExtOp[2]));  // open: gt, lt
  Comparator #(.width(7)) comparator_6 (.a(opcode), .b(7'b1100111), .eq(J_jalr));  // open: gt, lt
  Comparator #(.width(7)) comparator_7 (.a(opcode), .b(7'b1100011), .eq(B_beq___B_bgeu));  // open: gt, lt
  Comparator #(.width(7)) comparator_8 (.a(opcode), .b(7'b0000011), .eq(MemtoReg));  // open: gt, lt
  Comparator #(.width(7)) comparator_9 (.a(opcode), .b(7'b0100011), .eq(MemWr));  // open: gt, lt
  Comparator #(.width(7)) comparator_10 (.a(opcode), .b(7'b1110011), .eq(Halt));  // open: gt, lt
  and and_1 (and_1_out, I_addi___I_srai, comparator_11_eq);
  Comparator #(.width(3), .mode("unsigned")) comparator_11 (
    .a(funct3), .b(3'b101), .eq(comparator_11_eq));  // open: gt, lt
  Multiplexer #(.enable("false")) multiplexer_1 (
    .in0(1'b0), .in1(funct7[5]), .out(multiplexer_1_out[3]), .sel(or_1_out));
  or or_1 (or_1_out, and_1_out, R_add___R_and);
  or or_2 (ExtOp[0], U_lui, U_auipc, B_beq___B_bgeu);
  or or_3 (ExtOp[1], B_beq___B_bgeu, MemWr);
  or or_4 (ALUASrc, ExtOp[2], J_jalr, U_auipc);
  or or_5 (ALUBSrc[0], ExtOp[2], J_jalr);
  or or_6 (RegWr, U_lui, U_auipc, J_jalr, R_add___R_and, ExtOp[2], I_addi___I_srai, MemtoReg);
  or or_7 (ALUBSrc[1], MemtoReg, U_lui, I_addi___I_srai, MemWr, U_auipc);
  Multiplexer #(.width(4), .enable("false")) multiplexer_2 (
    .in0(4'b0000), .in1(4'b1111), .out(multiplexer_2_out), .sel(U_lui));
  Multiplexer #(.width(4), .enable("false")) multiplexer_3 (
    .in0({3'b001, funct3[1]}), .in1({multiplexer_1_out[3], funct3}), .out(multiplexer_3_out), .sel(or_8_out));
  or or_8 (or_8_out, I_addi___I_srai, R_add___R_and);
  Multiplexer #(.width(4), .enable("false")) multiplexer_4 (
    .in0(multiplexer_2_out), .in1(multiplexer_3_out), .out(ALUctr), .sel(or_9_out));
  or or_9 (or_9_out, or_8_out, B_beq___B_bgeu);
  or or_10 (or_11_out[1], ExtOp[2], J_jalr);
  Multiplexer #(.select(3), .width(3), .enable("false")) multiplexer_5 (
    .in0(3'b100), .in1(3'b101), .in4(3'b110), .in5(3'b111), .in6(3'b110), .in7(3'b111),
    .out(multiplexer_5_out), .sel(funct3));  // open: in2, in3
  or or_11 (or_11_out[0], J_jalr, B_beq___B_bgeu);
  Multiplexer #(.select(3), .width(3), .enable("false")) multiplexer_6 (
    .in0(3'b101), .in1(3'b110), .in2(3'b000), .in3(3'b000), .in4(3'b001), .in5(3'b010),
    .out(multiplexer_6_out), .sel(funct3));  // open: in6, in7
  or or_12 (or_12_out, MemWr, MemtoReg);
  Multiplexer #(.select(2), .width(3), .enable("false")) multiplexer_7 (
    .in0(3'b000), .in1(multiplexer_5_out), .in2(3'b001), .in3(3'b010), .out(BandJ), .sel(or_11_out));
  Multiplexer #(.width(3), .enable("false")) multiplexer_8 (
    .in0(3'b000), .in1(multiplexer_6_out), .out(MemOp), .sel(or_12_out));

  // Other names for the same wires on the sheet: J_jal = ExtOp[2]; I_lb___I_lhu = MemtoReg; S_sb___S_sw = MemWr

  // Notes on the sheet:
  //   输入引脚
  //   请勿修改引脚名称、电路名称及电路封装外观
  //   提示：根据指令种类，把7位指令code用一位指令类型标志位来表示，再通过功能码来区分具体指令，生成控制信号。
  //   输出引脚
endmodule

module IDU (
  input  [31:0] IR,
  input  [31:0] BusW,
  input  [31:0] PC,
  input  [2:0] ExtOp,
  input  RegWr,
  input  ALUASrc,
  input  [1:0] ALUBSrc,
  input  CLK,
  output [31:0] DataA,
  output [31:0] DataB,
  output [31:0] BusA,
  output [31:0] BusB,
  output [6:0] OpCode,
  output [31:0] Imm,
  output [2:0] Funct3,
  output [6:0] Funct7
);

  \立即数扩展器  \u_立即数扩展器_1  (.Instr(IR), .Extop(ExtOp), .imm(Imm));
  RegFile regfile_1 (
    .R1_num(IR[19:15]), .R2_num(IR[24:20]), .Write_Reg_num(IR[11:7]), .Din(BusW), .Reg1Out(BusA),
    .Reg2Out(BusB), .Write_Enable(RegWr), .Clock(CLK));
  Multiplexer #(.width(32), .enable("false")) multiplexer_1 (.in0(BusA), .in1(PC), .out(DataA), .sel(ALUASrc));
  Multiplexer #(.select(2), .width(32), .enable("false")) multiplexer_2 (
    .in0(BusB), .in1(32'h4), .in2(Imm), .out(DataB), .sel(ALUBSrc));  // open: in3

  assign Funct3 = IR[14:12];
  assign Funct7 = IR[31:25];
  assign OpCode = IR[6:0];

  // Other names for the same wires on the sheet: op[6:0] = IR[6:0]

  // Notes on the sheet:
  //   BusW: pull=down
  //   ALUBSrc: pull=down
  //   RegWr: pull=down
  //   PC: pull=down
  //   ExtOp: pull=down
  //   ALUASrc: pull=down
  //   输入信号
  //   为了后续实验中的引用，不要修改ALUASrc、ALUBSrc和EXtOP编码定义。
  //   请勿修改引脚名称、电路名称及电路封装外观
  //   输出信号
  //   修改寄存器堆电路设计，0号寄存器始终为0。
endmodule

module RegFile (
  input  [4:0] R1_num,
  input  [4:0] R2_num,
  input  [4:0] Write_Reg_num,
  input  [31:0] Din,
  input  Write_Enable,
  input  Clock,
  output [31:0] Reg1Out,
  output [31:0] Reg2Out
);

  wire and_2_out, and_3_out, and_4_out, and_5_out, and_6_out, and_7_out, and_8_out, and_9_out, and_10_out,
       and_11_out, and_12_out, and_13_out, and_14_out, and_15_out, and_16_out, and_17_out, and_18_out,
       and_19_out, and_20_out, and_21_out, and_22_out, and_23_out, and_24_out, and_25_out, and_26_out,
       and_27_out, and_28_out, and_29_out, and_30_out, and_31_out, and_32_out, decoder_1_out0,
       decoder_1_out1, decoder_1_out2, decoder_1_out3, decoder_1_out4, decoder_1_out5, decoder_1_out6,
       decoder_1_out7, decoder_1_out8, decoder_1_out9, decoder_1_out10, decoder_1_out11, decoder_1_out12,
       decoder_1_out13, decoder_1_out14, decoder_1_out15, decoder_1_out16, decoder_1_out17, decoder_1_out18,
       decoder_1_out19, decoder_1_out20, decoder_1_out21, decoder_1_out22, decoder_1_out23, decoder_1_out24,
       decoder_1_out25, decoder_1_out26, decoder_1_out27, decoder_1_out28, decoder_1_out29, decoder_1_out30,
       decoder_1_out31;
  wire [31:0] _0_q, _1_q, _2_q, _3_q, _4_q, _5_q, _6_q, _7_q, _8_q, _9_q, register_1_q, register_2_q,
       register_3_q, register_4_q, register_5_q, register_6_q, register_7_q, register_8_q, register_9_q,
       register_10_q, register_11_q, register_12_q, register_13_q, register_14_q, register_15_q,
       register_16_q, register_17_q, register_18_q, register_19_q, register_20_q, register_21_q,
       register_22_q;

  Decoder #(.select(5), .enable("false")) decoder_1 (
    .out0(decoder_1_out0), .out1(decoder_1_out1), .out2(decoder_1_out2), .out3(decoder_1_out3),
    .out4(decoder_1_out4), .out5(decoder_1_out5), .out6(decoder_1_out6), .out7(decoder_1_out7),
    .out8(decoder_1_out8), .out9(decoder_1_out9), .out10(decoder_1_out10), .out11(decoder_1_out11),
    .out12(decoder_1_out12), .out13(decoder_1_out13), .out14(decoder_1_out14), .out15(decoder_1_out15),
    .out16(decoder_1_out16), .out17(decoder_1_out17), .out18(decoder_1_out18), .out19(decoder_1_out19),
    .out20(decoder_1_out20), .out21(decoder_1_out21), .out22(decoder_1_out22), .out23(decoder_1_out23),
    .out24(decoder_1_out24), .out25(decoder_1_out25), .out26(decoder_1_out26), .out27(decoder_1_out27),
    .out28(decoder_1_out28), .out29(decoder_1_out29), .out30(decoder_1_out30), .out31(decoder_1_out31),
    .sel(Write_Reg_num));
  // AND_Gate and_1 has open pins: in0=Write_Enable, in1=decoder_1_out0, out=open
  and and_2 (and_2_out, Write_Enable, decoder_1_out1);
  and and_3 (and_3_out, Write_Enable, decoder_1_out2);
  and and_4 (and_4_out, Write_Enable, decoder_1_out3);
  and and_5 (and_5_out, Write_Enable, decoder_1_out4);
  and and_6 (and_6_out, Write_Enable, decoder_1_out5);
  and and_7 (and_7_out, Write_Enable, decoder_1_out6);
  and and_8 (and_8_out, Write_Enable, decoder_1_out7);
  and and_9 (and_9_out, Write_Enable, decoder_1_out8);
  and and_10 (and_10_out, Write_Enable, decoder_1_out9);
  and and_11 (and_11_out, Write_Enable, decoder_1_out10);
  and and_12 (and_12_out, Write_Enable, decoder_1_out11);
  and and_13 (and_13_out, Write_Enable, decoder_1_out12);
  and and_14 (and_14_out, Write_Enable, decoder_1_out13);
  and and_15 (and_15_out, Write_Enable, decoder_1_out14);
  and and_16 (and_16_out, Write_Enable, decoder_1_out15);
  and and_17 (and_17_out, Write_Enable, decoder_1_out16);
  and and_18 (and_18_out, Write_Enable, decoder_1_out17);
  and and_19 (and_19_out, Write_Enable, decoder_1_out18);
  and and_20 (and_20_out, Write_Enable, decoder_1_out19);
  and and_21 (and_21_out, Write_Enable, decoder_1_out20);
  and and_22 (and_22_out, Write_Enable, decoder_1_out21);
  and and_23 (and_23_out, Write_Enable, decoder_1_out22);
  and and_24 (and_24_out, Write_Enable, decoder_1_out23);
  and and_25 (and_25_out, Write_Enable, decoder_1_out24);
  and and_26 (and_26_out, Write_Enable, decoder_1_out25);
  and and_27 (and_27_out, Write_Enable, decoder_1_out26);
  and and_28 (and_28_out, Write_Enable, decoder_1_out27);
  and and_29 (and_29_out, Write_Enable, decoder_1_out28);
  and and_30 (and_30_out, Write_Enable, decoder_1_out29);
  and and_31 (and_31_out, Write_Enable, decoder_1_out30);
  and and_32 (and_32_out, Write_Enable, decoder_1_out31);
  Register #(.width(32), .Select("low")) _0 (.D(Din), .en(1'b0), .Q(_0_q), .clr(1'b1));  // open: clk
  Register #(.width(32), .Select("low")) _1 (.D(Din), .en(and_2_out), .Q(_1_q), .clk(Clock));  // open: clr
  Register #(.width(32), .Select("low")) _2 (.D(Din), .en(and_3_out), .Q(_2_q), .clk(Clock));  // open: clr
  Register #(.width(32), .Select("low")) _3 (.D(Din), .en(and_4_out), .Q(_3_q), .clk(Clock));  // open: clr
  Register #(.width(32), .Select("low")) _4 (.D(Din), .en(and_5_out), .Q(_4_q), .clk(Clock));  // open: clr
  Register #(.width(32), .Select("low")) _5 (.D(Din), .en(and_6_out), .Q(_5_q), .clk(Clock));  // open: clr
  Register #(.width(32), .Select("low")) _6 (.D(Din), .en(and_7_out), .Q(_6_q), .clk(Clock));  // open: clr
  Register #(.width(32), .Select("low")) _7 (.D(Din), .en(and_8_out), .Q(_7_q), .clk(Clock));  // open: clr
  Register #(.width(32), .Select("low")) _8 (.D(Din), .en(and_9_out), .Q(_8_q), .clk(Clock));  // open: clr
  Register #(.width(32), .Select("low")) _9 (.D(Din), .en(and_10_out), .Q(_9_q), .clk(Clock));  // open: clr
  Register #(.width(32), .Select("low")) register_1 (
    .D(Din), .en(and_11_out), .Q(register_1_q), .clk(Clock));  // open: clr
  Register #(.width(32), .Select("low")) register_2 (
    .D(Din), .en(and_12_out), .Q(register_2_q), .clk(Clock));  // open: clr
  Register #(.width(32), .Select("low")) register_3 (
    .D(Din), .en(and_13_out), .Q(register_3_q), .clk(Clock));  // open: clr
  Register #(.width(32), .Select("low")) register_4 (
    .D(Din), .en(and_14_out), .Q(register_4_q), .clk(Clock));  // open: clr
  Register #(.width(32), .Select("low")) register_5 (
    .D(Din), .en(and_15_out), .Q(register_5_q), .clk(Clock));  // open: clr
  Register #(.width(32), .Select("low")) register_6 (
    .D(Din), .en(and_16_out), .Q(register_6_q), .clk(Clock));  // open: clr
  Register #(.width(32), .Select("low")) register_7 (
    .D(Din), .en(and_17_out), .Q(register_7_q), .clk(Clock));  // open: clr
  Register #(.width(32), .Select("low")) register_8 (
    .D(Din), .en(and_18_out), .Q(register_8_q), .clk(Clock));  // open: clr
  Register #(.width(32), .Select("low")) register_9 (
    .D(Din), .en(and_19_out), .Q(register_9_q), .clk(Clock));  // open: clr
  Register #(.width(32), .Select("low")) register_10 (
    .D(Din), .en(and_20_out), .Q(register_10_q), .clk(Clock));  // open: clr
  Register #(.width(32), .Select("low")) register_11 (
    .D(Din), .en(and_21_out), .Q(register_11_q), .clk(Clock));  // open: clr
  Register #(.width(32), .Select("low")) register_12 (
    .D(Din), .en(and_22_out), .Q(register_12_q), .clk(Clock));  // open: clr
  Register #(.width(32), .Select("low")) register_13 (
    .D(Din), .en(and_23_out), .Q(register_13_q), .clk(Clock));  // open: clr
  Register #(.width(32), .Select("low")) register_14 (
    .D(Din), .en(and_24_out), .Q(register_14_q), .clk(Clock));  // open: clr
  Register #(.width(32), .Select("low")) register_15 (
    .D(Din), .en(and_25_out), .Q(register_15_q), .clk(Clock));  // open: clr
  Register #(.width(32), .Select("low")) register_16 (
    .D(Din), .en(and_26_out), .Q(register_16_q), .clk(Clock));  // open: clr
  Register #(.width(32), .Select("low")) register_17 (
    .D(Din), .en(and_27_out), .Q(register_17_q), .clk(Clock));  // open: clr
  Register #(.width(32), .Select("low")) register_18 (
    .D(Din), .en(and_28_out), .Q(register_18_q), .clk(Clock));  // open: clr
  Register #(.width(32), .Select("low")) register_19 (
    .D(Din), .en(and_29_out), .Q(register_19_q), .clk(Clock));  // open: clr
  Register #(.width(32), .Select("low")) register_20 (
    .D(Din), .en(and_30_out), .Q(register_20_q), .clk(Clock));  // open: clr
  Register #(.width(32), .Select("low")) register_21 (
    .D(Din), .en(and_31_out), .Q(register_21_q), .clk(Clock));  // open: clr
  Register #(.width(32), .Select("low")) register_22 (
    .D(Din), .en(and_32_out), .Q(register_22_q), .clk(Clock));  // open: clr
  Multiplexer #(.select(5), .width(32), .enable("false")) multiplexer_1 (
    .in0(_0_q), .in1(_1_q), .in2(_2_q), .in3(_3_q), .in4(_4_q), .in5(_5_q), .in6(_6_q), .in7(_7_q),
    .in8(_8_q), .in9(_9_q), .in10(register_1_q), .in11(register_2_q), .in12(register_3_q),
    .in13(register_4_q), .in14(register_5_q), .in15(register_6_q), .in16(register_7_q), .in17(register_8_q),
    .in18(register_9_q), .in19(register_10_q), .in20(register_11_q), .in21(register_12_q),
    .in22(register_13_q), .in23(register_14_q), .in24(register_15_q), .in25(register_16_q),
    .in26(register_17_q), .in27(register_18_q), .in28(register_19_q), .in29(register_20_q),
    .in30(register_21_q), .in31(register_22_q), .out(Reg1Out), .sel(R1_num));
  Multiplexer #(.select(5), .width(32), .enable("false")) multiplexer_2 (
    .in0(_0_q), .in1(_1_q), .in2(_2_q), .in3(_3_q), .in4(_4_q), .in5(_5_q), .in6(_6_q), .in7(_7_q),
    .in8(_8_q), .in9(_9_q), .in10(register_1_q), .in11(register_2_q), .in12(register_3_q),
    .in13(register_4_q), .in14(register_5_q), .in15(register_6_q), .in16(register_7_q), .in17(register_8_q),
    .in18(register_9_q), .in19(register_10_q), .in20(register_11_q), .in21(register_12_q),
    .in22(register_13_q), .in23(register_14_q), .in24(register_15_q), .in25(register_16_q),
    .in26(register_17_q), .in27(register_18_q), .in28(register_19_q), .in29(register_20_q),
    .in30(register_21_q), .in31(register_22_q), .out(Reg2Out), .sel(R2_num));

  // Other names for the same wires on the sheet: CLK = Clock; RA[4:0] = R1_num; RB[4:0] = R2_num; RDA[31:0] = Reg1Out;
  //   RDB[31:0] = Reg2Out; RW[4:0] = Write_Reg_num; WE = Write_Enable

  // Notes on the sheet:
  //   输入引脚
  //   请勿修改引脚名称、电路名称及电路封装外观
  //   提示：使用译码器、多路选择器和32位寄存器及逻辑门实现寄存器堆，禁止直接使用存储器组件。
  //   输出引脚
endmodule

module \立即数扩展器  (
  input  [31:0] Instr,
  input  [2:0] Extop,
  output [31:0] imm
);

  wire [11:0] bit_extender_3_out;
  wire [19:0] bit_extender_2_out;
  wire [31:0] bit_extender_1_out, bit_extender_4_out;

  assign bit_extender_1_out = {{20{Instr[31]}}, Instr[31:20]};  // Bit_Extender bit_extender_1
  assign bit_extender_2_out = {{19{Instr[31]}}, Instr[31]};  // Bit_Extender bit_extender_2
  assign bit_extender_3_out = {{11{Instr[31]}}, Instr[31]};  // Bit_Extender bit_extender_3
  assign bit_extender_4_out = {{20{Instr[31]}}, {Instr[31:25], Instr[11:7]}};  // Bit_Extender bit_extender_4
  Multiplexer #(.select(3), .width(32), .enable("false")) multiplexer_1 (
    .in0(bit_extender_1_out), .in1({Instr[31:12], {12{1'b0}}}), .in2(bit_extender_4_out),
    .in3({bit_extender_2_out, Instr[7], Instr[30:25], Instr[11:8], 1'b0}),
    .in4({bit_extender_3_out, Instr[19:12], Instr[20], Instr[30:21], 1'b0}), .out(imm), .sel(Extop));  // open: in5, in6, in7

  // Notes on the sheet:
  //   Instr: pull=down
  //   Extop: pull=down
  //   输入引脚
  //   请勿修改引脚名称、电路名称及电路封装外观
  //   提示：使用分线器和多路选择器实现立即数扩展器
  //   输出引脚
endmodule

module DataRAM (
  input  CLK,
  input  CLR,
  input  WE,
  input  [2:0] MemOp,
  input  [17:0] Addr,
  input  [31:0] Din,
  output AlignErr,
  output [31:0] DataOut
);

  wire and_1_out, and_2_out, and_3_out, and_4_out, and_5_out, and_6_out, and_7_out, and_8_out, and_9_out,
       and_10_out, and_11_out, and_12_out, and_13_out, and_14_out, not_1_out;
  wire [3:0] SEL;
  wire [7:0] IN0, IN1, IN2, IN3, OUT0, OUT1, OUT2, OUT3;
  wire [31:0] bit_extender_1_out, bit_extender_2_out, bit_extender_3_out, bit_extender_4_out,
       bit_extender_5_out, bit_extender_6_out, bit_extender_7_out, bit_extender_8_out, bit_extender_9_out,
       bit_extender_10_out, bit_extender_11_out, bit_extender_12_out, multiplexer_1_out, multiplexer_2_out,
       multiplexer_3_out, multiplexer_4_out, multiplexer_5_out, multiplexer_6_out;

  and and_1 (and_1_out, ~Addr[0], ~Addr[1]);  // AND_Gate
  and and_2 (and_2_out, Addr[0], ~Addr[1]);  // AND_Gate
  and and_3 (and_3_out, ~Addr[0], Addr[1]);  // AND_Gate
  and and_4 (and_4_out, Addr[0], Addr[1]);
  and and_5 (and_5_out, ~MemOp[0], ~MemOp[1], ~MemOp[2]);  // AND_Gate
  and and_6 (and_6_out, MemOp[0], ~MemOp[1]);  // AND_Gate
  and and_7 (and_7_out, ~MemOp[0], MemOp[1]);  // AND_Gate
  not not_1 (not_1_out, MemOp[2]);
  assign bit_extender_1_out = {{24{1'b0}}, OUT0};  // Bit_Extender bit_extender_1
  assign bit_extender_2_out = {{24{1'b0}}, OUT1};  // Bit_Extender bit_extender_2
  assign bit_extender_3_out = {{24{1'b0}}, OUT2};  // Bit_Extender bit_extender_3
  assign bit_extender_4_out = {{24{1'b0}}, OUT3};  // Bit_Extender bit_extender_4
  assign bit_extender_5_out = {{16{1'b0}}, {OUT1, OUT0}};  // Bit_Extender bit_extender_5
  assign bit_extender_6_out = {{16{1'b0}}, {OUT3, OUT2}};  // Bit_Extender bit_extender_6
  RAM #(.addrWidth(16), .bus("separate"), .Select("high"), .simpleMode("false")) ram_1 (
    .addr(Addr[17:2]), .din(IN3), .data(OUT3), .str(WE), .sel(SEL[3]), .clk(CLK), .clr(CLR));  // open: ld
  and and_8 (and_8_out, and_5_out, and_1_out);
  and and_9 (and_9_out, and_6_out, and_1_out);
  and and_10 (and_10_out, and_6_out, and_2_out);
  and and_11 (and_11_out, and_6_out, and_3_out);
  and and_12 (and_12_out, and_6_out, and_4_out);
  and and_13 (and_13_out, and_7_out, and_1_out);
  and and_14 (and_14_out, and_7_out, and_3_out);
  assign bit_extender_7_out = {{24{OUT0[7]}}, OUT0};  // Bit_Extender bit_extender_7
  assign bit_extender_8_out = {{24{OUT1[7]}}, OUT1};  // Bit_Extender bit_extender_8
  assign bit_extender_9_out = {{24{OUT2[7]}}, OUT2};  // Bit_Extender bit_extender_9
  assign bit_extender_10_out = {{24{OUT3[7]}}, OUT3};  // Bit_Extender bit_extender_10
  assign bit_extender_11_out = {{16{OUT1[7]}}, {OUT1, OUT0}};  // Bit_Extender bit_extender_11
  assign bit_extender_12_out = {{16{OUT3[7]}}, {OUT3, OUT2}};  // Bit_Extender bit_extender_12
  Multiplexer #(.width(32), .enable("false")) multiplexer_1 (
    .in0(bit_extender_7_out), .in1(bit_extender_1_out), .out(multiplexer_1_out), .sel(not_1_out));
  Multiplexer #(.width(32), .enable("false")) multiplexer_2 (
    .in0(bit_extender_8_out), .in1(bit_extender_2_out), .out(multiplexer_2_out), .sel(not_1_out));
  Multiplexer #(.width(32), .enable("false")) multiplexer_3 (
    .in0(bit_extender_9_out), .in1(bit_extender_3_out), .out(multiplexer_3_out), .sel(not_1_out));
  Multiplexer #(.width(32), .enable("false")) multiplexer_4 (
    .in0(bit_extender_10_out), .in1(bit_extender_4_out), .out(multiplexer_4_out), .sel(not_1_out));
  Multiplexer #(.width(32), .enable("false")) multiplexer_5 (
    .in0(bit_extender_11_out), .in1(bit_extender_5_out), .out(multiplexer_5_out), .sel(not_1_out));
  Multiplexer #(.width(32), .enable("false")) multiplexer_6 (
    .in0(bit_extender_12_out), .in1(bit_extender_6_out), .out(multiplexer_6_out), .sel(not_1_out));
  or or_1 (SEL[0], and_8_out, and_13_out, and_9_out);
  or or_2 (SEL[1], and_8_out, and_13_out, and_10_out);
  or or_3 (SEL[2], and_8_out, and_14_out, and_11_out);
  or or_4 (SEL[3], and_8_out, and_14_out, and_12_out);
  nor nor_1 (AlignErr, and_8_out, and_14_out, and_9_out, and_10_out, and_11_out, and_12_out, and_13_out);
  Multiplexer #(.select(4), .width(32), .enable("false")) multiplexer_7 (
    .in1(multiplexer_1_out), .in2(multiplexer_2_out), .in3(multiplexer_5_out), .in4(multiplexer_3_out),
    .in8(multiplexer_4_out), .in12(multiplexer_6_out), .in15({OUT3, OUT2, OUT1, OUT0}), .out(DataOut),
    .sel(SEL));  // open: in0, in5, in6, in7, in9, in10, in11, in13, in14
  RAM #(.addrWidth(16), .bus("separate"), .Select("high"), .simpleMode("false")) ram_2 (
    .addr(Addr[17:2]), .din(IN2), .data(OUT2), .str(WE), .sel(SEL[2]), .clk(CLK), .clr(CLR));  // open: ld
  RAM #(.addrWidth(16), .bus("separate"), .Select("high"), .simpleMode("false")) ram_3 (
    .addr(Addr[17:2]), .din(IN1), .data(OUT1), .str(WE), .sel(SEL[1]), .clk(CLK), .clr(CLR));  // open: ld
  Multiplexer #(.select(4), .width(8), .enable("false")) multiplexer_8 (
    .in1(Din[7:0]), .in3(Din[7:0]), .in15(Din[7:0]), .out(IN0), .sel(SEL));  // open: in0, in2, in4, in5, in6, in7, in8, in9, in10, in11, in12, in13, in14
  Multiplexer #(.select(4), .width(8), .enable("false")) multiplexer_9 (
    .in2(Din[7:0]), .in3(Din[15:8]), .in15(Din[15:8]), .out(IN1), .sel(SEL));  // open: in0, in1, in4, in5, in6, in7, in8, in9, in10, in11, in12, in13, in14
  Multiplexer #(.select(4), .width(8), .enable("false")) multiplexer_10 (
    .in4(Din[7:0]), .in12(Din[7:0]), .in15(Din[23:16]), .out(IN2), .sel(SEL));  // open: in0, in1, in2, in3, in5, in6, in7, in8, in9, in10, in11, in13, in14
  Multiplexer #(.select(4), .width(8), .enable("false")) multiplexer_11 (
    .in8(Din[7:0]), .in12(Din[15:8]), .in15(Din[31:24]), .out(IN3), .sel(SEL));  // open: in0, in1, in2, in3, in4, in5, in6, in7, in9, in10, in11, in13, in14
  RAM #(.addrWidth(16), .bus("separate"), .Select("high"), .simpleMode("false")) ram_4 (
    .addr(Addr[17:2]), .din(IN0), .data(OUT0), .str(WE), .sel(SEL[0]), .clk(CLK), .clr(CLR));  // open: ld

  // Other names for the same wires on the sheet: Dout[31:0] = DataOut

  // Notes on the sheet:
  //   输入引脚
  //   请勿修改引脚名称、电路名称及电路封装外观
  //   为了后续实验中的引用，不要修改MemOp的编码定义、引脚名称和在布局中的位置。
  //   32位数据存储器，按字节分4片存储，可按照字节、半字和字进行存储；读取字节或半字时，支持0扩展和符号位扩展。
  //   输出引脚
endmodule

module ALU (
  input  [3:0] ALUctr,
  input  [31:0] A,
  input  [31:0] B,
  output Zero,
  output [31:0] S
);

  wire adder32_1_cf, adder32_1_of, adder32_1_sf, aluctrl_1_alctr, aluctrl_1_sftctr, aluctrl_1_sigctr,
       aluctrl_1_subctr, multiplexer_2_out, xor_3_out;
  wire [2:0] aluctrl_1_opctr;
  wire [31:0] adder32_1_s, and_1_out, bit_extender_1_out, bit_extender_2_out, or_1_out, shifter32_1_dataout,
       xor_1_out, xor_2_out;

  assign bit_extender_1_out = {{31{aluctrl_1_subctr}}, aluctrl_1_subctr};  // Bit_Extender bit_extender_1
  assign and_1_out = A & B;  // AND_Gate and_1, 32 bits wide
  assign or_1_out = A | B;  // OR_Gate or_1, 32 bits wide
  Adder32 adder32_1 (
    .CF(adder32_1_cf), .OF(adder32_1_of), .SF(adder32_1_sf), .ZF(Zero), .X(A), .Y(xor_1_out),
    .Cin(aluctrl_1_subctr), .S(adder32_1_s));  // open: Cout
  assign xor_1_out = B ^ bit_extender_1_out;  // XOR_Gate xor_1, 32 bits wide
  assign xor_2_out = A ^ B;  // XOR_Gate xor_2, 32 bits wide
  Shifter32 shifter32_1 (
    .DataIn(A), .shamt(B[4:0]), .L_R(aluctrl_1_sftctr), .A_L(aluctrl_1_alctr), .DataOut(shifter32_1_dataout));
  xor xor_3 (xor_3_out, adder32_1_of, adder32_1_sf);
  assign bit_extender_2_out = {{31{1'b0}}, multiplexer_2_out};  // Bit_Extender bit_extender_2
  Multiplexer #(.select(3), .width(32), .enable("false")) multiplexer_1 (
    .in0(adder32_1_s), .in1(and_1_out), .in2(or_1_out), .in3(xor_2_out), .in4(shifter32_1_dataout), .in5(B),
    .in6(bit_extender_2_out), .out(S), .sel(aluctrl_1_opctr));  // open: in7
  Multiplexer #(.enable("false")) multiplexer_2 (
    .in0(adder32_1_cf), .in1(xor_3_out), .out(multiplexer_2_out), .sel(aluctrl_1_sigctr));
  ALUctrl aluctrl_1 (
    .SUBctr(aluctrl_1_subctr), .SFTctr(aluctrl_1_sftctr), .SIGctr(aluctrl_1_sigctr), .ALctr(aluctrl_1_alctr),
    .OPctr(aluctrl_1_opctr), .ALUctr(ALUctr));
  // Probe on A
  // Probe on B
  // Probe on S

  // Other names for the same wires on the sheet: Result[31:0] = S

  // Notes on the sheet:
  //   ALUctr: pull=down
  //   B: pull=down
  //   A: pull=down
  //   输入引脚
  //   请勿修改引脚名称、电路名称及电路封装外观
  //   提示：使用32位并行加法器子电路、桶形移位器、ALU控制子电路实现32位ALU
  //   功能说明:32位ALU，输入32位操作数A、B，4位控制信号ALUctr，输出32位结果Reseult和1位Zero标志位
  //   输出引脚
  //   操作数和结果
endmodule

module ALUctrl (
  input  [3:0] ALUctr,
  output SUBctr,
  output SFTctr,
  output SIGctr,
  output ALctr,
  output [2:0] OPctr
);

  wire and_1_out, and_2_out, and_6_out, and_7_out, and_8_out, and_9_out, and_10_out, and_11_out;

  and and_1 (and_1_out, ~ALUctr[3], ~ALUctr[2], ALUctr[1]);  // AND_Gate
  or or_1 (SUBctr, and_1_out, and_2_out);
  and and_2 (and_2_out, ALUctr[3], ~ALUctr[2], ~ALUctr[1], ~ALUctr[0]);  // AND_Gate
  and and_3 (SIGctr, ~ALUctr[3], ~ALUctr[2], ALUctr[1], ~ALUctr[0]);  // AND_Gate
  and and_4 (ALctr, ALUctr[3], ALUctr[2], ~ALUctr[1], ALUctr[0]);  // AND_Gate
  and and_5 (SFTctr, ~ALUctr[3], ~ALUctr[2], ~ALUctr[1], ALUctr[0]);  // AND_Gate
  and and_6 (and_6_out, ~ALUctr[3], ~ALUctr[1], ALUctr[0]);  // AND_Gate
  and and_7 (and_7_out, ~ALUctr[3], ~ALUctr[2], ALUctr[1]);  // AND_Gate
  and and_8 (and_8_out, ALUctr[3], ALUctr[2], ALUctr[0]);
  and and_9 (and_9_out, ~ALUctr[3], ALUctr[2], ~ALUctr[0]);  // AND_Gate
  and and_10 (and_10_out, ALUctr[2], ALUctr[1], ALUctr[0]);
  and and_11 (and_11_out, ~ALUctr[3], ALUctr[2], ~ALUctr[1], ~ALUctr[0]);  // AND_Gate
  or or_2 (OPctr[2], and_6_out, and_7_out, and_8_out);
  or or_3 (OPctr[1], and_7_out, and_9_out);
  or or_4 (OPctr[0], and_10_out, and_11_out);

  // Other names for the same wires on the sheet: LRctr = SFTctr

  // Notes on the sheet:
  //   输入引脚
  //   ALU操作控制信号生成部件
  //   输出引脚
endmodule

module Adder32 (
  input  Cin,
  input  [31:0] X,
  input  [31:0] Y,
  output CF,
  output Cout,
  output OF,
  output SF,
  output [31:0] S,
  output ZF
);

  wire adder16_2_c16, and_1_out, and_2_out, and_3_out, and_4_out;

  xor xor_1 (CF, Cout, Cin);
  Adder16 adder16_1 (.X(X[31:16]), .Y(Y[31:16]), .C0(adder16_2_c16), .S(S[31:16]), .C16(Cout));  // open: Pg, Gg
  Comparator #(.width(32)) comparator_1 (.a(S), .b({32{1'b0}}), .eq(ZF));  // open: gt, lt
  Adder16 adder16_2 (.X(X[15:0]), .Y(Y[15:0]), .C0(Cin), .S(S[15:0]), .C16(adder16_2_c16));  // open: Pg, Gg
  and and_1 (and_1_out, ~S[31], and_2_out);  // AND_Gate
  and and_2 (and_2_out, Y[31], X[31]);
  and and_3 (and_3_out, S[31], and_4_out);
  and and_4 (and_4_out, ~X[31], ~Y[31]);  // AND_Gate
  or or_1 (OF, and_1_out, and_3_out);
  // Probe on X
  // Probe on Y
  // Probe on S

  assign SF = S[31];

  // Notes on the sheet:
  //   Y: pull=down
  //   Cin: pull=down
  //   X: pull=down
  //   输入引脚区
  //   输出引脚区
  //   请勿修改引脚名称、电路名称及电路封装外观
  //   提示：使用16位并行加法器子电路实现32位快速加法器
  //   功能说明:32位Adder  S=X+Y，Cout为最高位进位位，Cin为进位输入， S为和，溢出OF、进位CF、零ZF、符号SF。
  //   +
  //   =
  //   无符号加法
endmodule

// 移位器
module Shifter32 (
  input  [4:0] shamt,
  input  L_R,
  input  A_L,
  input  [31:0] DataIn,
  output [31:0] DataOut
);

  wire [0:0] multiplexer_2_out;
  wire [1:0] multiplexer_4_out;
  wire [3:0] multiplexer_6_out;
  wire [7:0] multiplexer_8_out;
  wire [15:0] multiplexer_10_out;
  wire [31:0] multiplexer_3_out, multiplexer_5_out, multiplexer_7_out, multiplexer_9_out;
  wire [31:31] multiplexer_1_out;

  Multiplexer #(.enable("false")) multiplexer_1 (.in0(1'b0), .in1(DataIn[31]), .out(multiplexer_1_out[31]), .sel(A_L));
  Multiplexer #(.enable("false")) multiplexer_2 (.in0(1'b0), .in1(DataIn[31]), .out(multiplexer_2_out[0]), .sel(A_L));
  Multiplexer #(.select(2), .width(32), .enable("false")) multiplexer_3 (
    .in0(DataIn), .in1({multiplexer_1_out[31], DataIn[31:1]}), .in2(DataIn),
    .in3({DataIn[30:0], multiplexer_2_out[0]}), .out(multiplexer_3_out), .sel({L_R, shamt[0]}));
  Multiplexer #(.width(2), .enable("false")) multiplexer_4 (
    .in0(2'b00), .in1(multiplexer_3_out[31:30]), .out(multiplexer_4_out), .sel(A_L));
  Multiplexer #(.select(2), .width(32), .enable("false")) multiplexer_5 (
    .in0(multiplexer_3_out), .in1({{2{multiplexer_1_out[31]}}, multiplexer_3_out[31:2]}),
    .in2(multiplexer_3_out), .in3({multiplexer_3_out[29:0], multiplexer_4_out}), .out(multiplexer_5_out),
    .sel({L_R, shamt[1]}));
  Multiplexer #(.width(4), .enable("false")) multiplexer_6 (
    .in0(4'b0000), .in1(multiplexer_5_out[31:28]), .out(multiplexer_6_out), .sel(A_L));
  Multiplexer #(.select(2), .width(32), .enable("false")) multiplexer_7 (
    .in0(multiplexer_5_out), .in1({{4{multiplexer_1_out[31]}}, multiplexer_5_out[31:4]}),
    .in2(multiplexer_5_out), .in3({multiplexer_5_out[27:0], multiplexer_6_out}), .out(multiplexer_7_out),
    .sel({L_R, shamt[2]}));
  Multiplexer #(.width(8), .enable("false")) multiplexer_8 (
    .in0({8{1'b0}}), .in1(multiplexer_7_out[31:24]), .out(multiplexer_8_out), .sel(A_L));
  Multiplexer #(.select(2), .width(32), .enable("false")) multiplexer_9 (
    .in0(multiplexer_7_out), .in1({{8{multiplexer_1_out[31]}}, multiplexer_7_out[31:8]}),
    .in2(multiplexer_7_out), .in3({multiplexer_7_out[23:0], multiplexer_8_out}), .out(multiplexer_9_out),
    .sel({L_R, shamt[3]}));
  Multiplexer #(.width(16), .enable("false")) multiplexer_10 (
    .in0({16{1'b0}}), .in1(multiplexer_9_out[31:16]), .out(multiplexer_10_out), .sel(A_L));
  Multiplexer #(.select(2), .width(32), .enable("false")) multiplexer_11 (
    .in0(multiplexer_9_out), .in1({{16{multiplexer_1_out[31]}}, multiplexer_9_out[31:16]}),
    .in2(multiplexer_9_out), .in3({multiplexer_9_out[15:0], multiplexer_10_out}), .out(DataOut),
    .sel({L_R, shamt[4]}));

  // Other names for the same wires on the sheet: Din[31:0] = DataIn; Left_Right = L_R; Arth_Logic = A_L;
  //   Dout[31:0] = DataOut

  // Notes on the sheet:
  //   L/R,A/L: 00逻辑右移，01算术右移，10逻辑左移，11：循环左移
  //   输入引脚
  //   请勿修改引脚名称、电路名称及电路封装外观
  //   提示：使用多路选择器、逻辑门实现32位桶形移位器，禁止直接使用移位器组件。
  //   输出引脚
endmodule

module Adder16 (
  input  C0,
  input  [15:0] X,
  input  [15:0] Y,
  output C16,
  output Pg,
  output Gg,
  output [15:0] S
);

  wire cla4_1_gg, cla4_1_pg, cla4_2_gg, cla4_2_pg, cla4_3_gg, cla4_3_pg, cla4_4_gg, cla4_4_pg, clu4_1_c1,
       clu4_1_c2, clu4_1_c3;

  CLA4 cla4_1 (.X(X[15:12]), .F(S[15:12]), .Cout(C16), .Y(Y[15:12]), .Pg(cla4_1_pg), .Cin(clu4_1_c3), .Gg(cla4_1_gg));
  CLU4 clu4_1 (
    .P0(cla4_4_pg), .P1(cla4_3_pg), .P2(cla4_2_pg), .P3(cla4_1_pg), .C1(clu4_1_c1), .C3(clu4_1_c3),
    .G0(cla4_4_gg), .G1(cla4_3_gg), .G2(cla4_2_gg), .G3(cla4_1_gg), .C2(clu4_1_c2), .C0(C0), .Pg(Pg), .Gg(Gg));  // open: C4
  CLA4 cla4_2 (.X(X[11:8]), .F(S[11:8]), .Y(Y[11:8]), .Pg(cla4_2_pg), .Cin(clu4_1_c2), .Gg(cla4_2_gg));  // open: Cout
  CLA4 cla4_3 (.X(X[7:4]), .F(S[7:4]), .Y(Y[7:4]), .Pg(cla4_3_pg), .Cin(clu4_1_c1), .Gg(cla4_3_gg));  // open: Cout
  CLA4 cla4_4 (.X(X[3:0]), .F(S[3:0]), .Y(Y[3:0]), .Pg(cla4_4_pg), .Cin(C0), .Gg(cla4_4_gg));  // open: Cout
  // Probe on X
  // Probe on Y
  // Probe on S

  // Notes on the sheet:
  //   Y: pull=down
  //   C0: pull=down
  //   X: pull=down
  //   输入引脚区
  //   请勿修改引脚名称、电路名称及电路封装外观
  //   提示：使用4位先行进位加法器和CLU子电路实现16位并行加法器
  //   功能说明:16位Adder  S=X+Y，C16为最高位进位位，C0为进位输入， Pg、Gg为成组进位生成传递函数
  //   输出引脚区
  //   +
  //   =
  //   无符号加法
endmodule

module CLA4 (
  input  [3:0] X,
  input  [3:0] Y,
  input  Cin,
  output [3:0] F,
  output Cout,
  output Pg,
  output Gg
);

  wire clu4_1_c1, clu4_1_c2, clu4_1_c3, fa_1_g, fa_1_p, fa_2_g, fa_2_p, fa_3_g, fa_3_p, fa_4_g, fa_4_p;

  FA fa_1 (.A(X[3]), .F(F[3]), .B(Y[3]), .P(fa_1_p), .Cin(clu4_1_c3), .G(fa_1_g));
  Hex_Digit_Display hex_digit_display_1 (.value(X));  // open: dp
  FA fa_2 (.A(X[2]), .F(F[2]), .B(Y[2]), .P(fa_2_p), .Cin(clu4_1_c2), .G(fa_2_g));
  Hex_Digit_Display hex_digit_display_2 (.value(Y));  // open: dp
  CLU4 clu4_1 (
    .P0(fa_4_p), .P1(fa_3_p), .P2(fa_2_p), .P3(fa_1_p), .C1(clu4_1_c1), .C3(clu4_1_c3), .G0(fa_4_g),
    .G1(fa_3_g), .G2(fa_2_g), .G3(fa_1_g), .C2(clu4_1_c2), .C4(Cout), .C0(Cin), .Pg(Pg), .Gg(Gg));
  FA fa_3 (.A(X[1]), .F(F[1]), .B(Y[1]), .P(fa_3_p), .Cin(clu4_1_c1), .G(fa_3_g));
  Hex_Digit_Display hex_digit_display_3 (.value(F));  // open: dp
  FA fa_4 (.A(X[0]), .F(F[0]), .B(Y[0]), .P(fa_4_p), .Cin(Cin), .G(fa_4_g));

  // Other names for the same wires on the sheet: Z[3:0] = F

  // Notes on the sheet:
  //   +
  //   =
  //   输出
  //   输入
  //   请勿修改引脚名称、电路名称及电路封装外观
  //   提示：使用全加器和CLU子电路实现四位先行进位加法器CLA4
endmodule

module CLU4 (
  input  P0,
  input  P1,
  input  P2,
  input  P3,
  input  G0,
  input  G1,
  input  G2,
  input  G3,
  input  C0,
  output C1,
  output C3,
  output C2,
  output C4,
  output Pg,
  output Gg
);

  wire and_2_out, and_3_out, and_4_out, and_5_out, and_6_out, and_7_out, and_8_out, and_9_out, and_10_out,
       and_11_out;

  or or_1 (Gg, G3, and_3_out, and_4_out, and_5_out);
  and and_1 (Pg, P0, P1, P2, P3);
  or or_2 (C4, Gg, and_2_out);
  and and_2 (and_2_out, Pg, C0);
  and and_3 (and_3_out, G0, P1, P2, P3);
  and and_4 (and_4_out, G1, P2, P3);
  and and_5 (and_5_out, G2, P3);
  or or_3 (C3, G2, and_6_out, and_8_out, and_7_out);
  and and_6 (and_6_out, C0, P0, P1, P2);
  and and_7 (and_7_out, G1, P2);
  and and_8 (and_8_out, G0, P1, P2);
  or or_4 (C2, G1, and_9_out, and_10_out);
  and and_9 (and_9_out, C0, P0, P1);
  and and_10 (and_10_out, G0, P1);
  or or_5 (C1, G0, and_11_out);
  and and_11 (and_11_out, C0, P0);

  // Notes on the sheet:
  //   输入引脚
  //   请勿修改引脚名称、电路名称及电路封装外观
  //   提示：使用逻辑门电路实现4位四位先行进位部件CLU，Pg、Gg为成组进位生成传递函数
  //   输出引脚
endmodule

module FA (
  input  A,
  input  B,
  input  Cin,
  output F,
  output P,
  output G
);

  wire xor_2_out;

  and and_1 (G, A, B);
  or or_1 (P, A, B);
  xor xor_1 (F, xor_2_out, Cin);
  xor xor_2 (xor_2_out, A, B);

  // Notes on the sheet:
  //   输入引脚
  //   请勿修改引脚名称、电路名称及电路封装外观
  //   输出引脚
endmodule
