// Logisim project lab8.1.circ as structural Verilog: 21 circuits, main circuit main
module main (
  input  [31:0] Init_Addr,
  input  ReSet,
  input  [31:0] BP_PC,
  input  BPEn,
  input  clk,
  output [31:0] WB_PC,
  output [31:0] WB_BusW,
  output [15:0] Cycles,
  output halt
);

  wire alu_1_zero, and_1_out, and_2_out, and_3_out, and_4_out, and_5_out, and_6_out, and_7_out, and_8_out,
       and_9_out, clk_out, clk_t, comparator_1_eq, comparator_2_eq, comparator_3_eq, comparator_4_eq,
       nor_1_out, nor_2_out, not_1_out, not_3_out, not_4_out, not_5_out, not_6_out, or_1_out, or_2_out,
       or_3_out, or_4_out, or_5_out, or_6_out, Stop, undriven, undriven_2, \控制器_1_aluasrc , \控制器_1_halt ,
       \控制器_1_memtoreg , \控制器_1_memwr , \控制器_1_regwr , \流水段寄存器_2_aluasrco , \流水段寄存器_2_halto ,
       \流水段寄存器_2_memtorego , \流水段寄存器_2_memwro , \流水段寄存器_2_regwro , \流水段寄存器_3_aluasrco , \流水段寄存器_3_halto ,
       \流水段寄存器_3_memtorego , \流水段寄存器_3_memwro , \流水段寄存器_3_regwro , \流水段寄存器_3_zeroo , \流水段寄存器_4_memtorego ,
       \流水段寄存器_4_regwro , \跳转检测_1_pcsrc , \阻塞检测_1_stall ;
  wire [1:0] \控制器_1_alubsrc , \流水段寄存器_2_alubsrco , \流水段寄存器_3_alubsrco , \转发检测_1_busafw , \转发检测_1_busbfw ;
  wire [2:0] idu_1_funct3, \控制器_1_bandj , \控制器_1_extop , \控制器_1_memop , \流水段寄存器_2_bandjo , \流水段寄存器_2_memopo ,
       \流水段寄存器_3_bandjo , \流水段寄存器_3_memopo ;
  wire [3:0] \控制器_1_aluctr , \流水段寄存器_2_aluctro , \流水段寄存器_3_aluctro ;
  wire [4:0] idu_1_rd, idu_1_rs1, idu_1_rs2, \流水段寄存器_2_rdo , \流水段寄存器_2_rs1o , \流水段寄存器_2_rs2o ,
       \流水段寄存器_3_rdo , \流水段寄存器_3_rs1o , \流水段寄存器_3_rs2o , \流水段寄存器_4_rdo ;
  wire [6:0] idu_1_funct7, idu_1_opcode;
  wire [13:0] \流水段寄存器_3_resulto_2 ;
  wire [15:0] \RS1转发次数 , \RS2转发次数 , \冲刷次数 , \分支指令数 , \跳转指令数 , \阻塞次数 ;
  wire [17:0] \流水段寄存器_3_resulto ;
  wire [31:0] adder_1_out, alu_1_s, dataram_1_dataout, EX_PC, ID_PC, idu_1_busa, idu_1_busb, idu_1_imm,
       IF_IR, IF_PC, M_PC, multiplexer_1_out, multiplexer_2_out, multiplexer_3_out, multiplexer_4_out,
       multiplexer_5_out, WB_IR, \流水段寄存器_1_iro , \流水段寄存器_2_busao , \流水段寄存器_2_busbo , \流水段寄存器_2_immo ,
       \流水段寄存器_2_iro , \流水段寄存器_3_busao , \流水段寄存器_3_busbo , \流水段寄存器_3_immo , \流水段寄存器_3_iro ,
       \流水段寄存器_3_pctargeto , \流水段寄存器_4_douto , \流水段寄存器_4_resulto ;

  and and_1 (and_1_out, ~Stop, and_3_out);  // AND_Gate
  Counter #(.width(16), .max('hffff)) counter_1 (
    .count(and_1_out), .Q(\RS1转发次数 ), .clk(clk_t), .clr(ReSet));  // open: load, D, carry, preset, down
  Clock u_clk (.out(clk_out));
  not not_1 (not_1_out, Stop);
  Counter #(.width(16), .max('hffff)) counter_2 (
    .count(not_1_out), .Q(Cycles), .clk(clk_t), .clr(ReSet), .down(undriven));  // open: load, D, carry, preset
  and and_2 (and_2_out, ~Stop, \跳转检测_1_pcsrc );  // AND_Gate
  Counter #(.width(16), .max('hffff)) counter_3 (
    .count(and_2_out), .Q(\冲刷次数 ), .clk(clk_t), .clr(ReSet));  // open: load, D, carry, preset, down
  and and_3 (and_3_out, or_2_out, ~\流水段寄存器_2_aluasrco );  // AND_Gate
  not not_2 (clk_t, clk_out);
  Comparator #(.width(32)) comparator_1 (.a(IF_PC), .b(BP_PC), .eq(comparator_1_eq));  // open: gt, lt
  IFU ifu_1 (
    .CLK(clk_t), .Reset(ReSet), .PCSrc(\跳转检测_1_pcsrc ), .Initial_Address(Init_Addr),
    .PCTarget(\流水段寄存器_3_pctargeto ), .PC(IF_PC), .halt(\控制器_1_halt ), .BPEn(BPEn), .BP_PC(BP_PC),
    .Stall(\阻塞检测_1_stall ));
  and and_4 (and_4_out, ~Stop, \阻塞检测_1_stall );  // AND_Gate
  Counter #(.width(16), .max('hffff)) counter_4 (
    .count(and_4_out), .Q(\阻塞次数 ), .clk(clk_t), .clr(ReSet), .down(undriven_2));  // open: load, D, carry, preset
  and and_5 (and_5_out, ~Stop, or_6_out);  // AND_Gate
  Counter #(.width(16), .max('hffff)) counter_5 (
    .count(and_5_out), .Q(\跳转指令数 ), .clk(clk_t), .clr(ReSet));  // open: load, D, carry, preset, down
  and and_6 (and_6_out, ~Stop, \流水段寄存器_3_bandjo [2]);  // AND_Gate
  Counter #(.width(16), .max('hffff)) counter_6 (
    .count(and_6_out), .Q(\分支指令数 ), .clk(clk_t), .clr(ReSet));  // open: load, D, carry, preset, down
  and and_7 (and_7_out, BPEn, comparator_1_eq);
  or or_1 (or_1_out, ReSet, \跳转检测_1_pcsrc );
  ROM #(.addrWidth(16), .dataWidth(32), .Select("high")) rom_1 (.addr(IF_PC[17:2]), .data(IF_IR));
  nor nor_1 (nor_1_out, \阻塞检测_1_stall , \控制器_1_halt , and_7_out);
  \流水段寄存器  \u_流水段寄存器_1  (
    .CLR(or_1_out), .CLK(clk_t), .WE(nor_1_out), .PC(IF_PC), .PCo(ID_PC), .IR(IF_IR), .IRo(\流水段寄存器_1_iro ));  // open: ALUctr, ALUctro, ALUASrc, ALUASrco, ALUBSrc, ALUBSrco, Halt, Halto, BandJ, BandJo, MemOp, MemOpo, MemWr, MemWro, RegWr, RegWro, MemtoReg, MemtoRego, RD, RDo, BusA, BusAo, RS1, RS1o, RS2, RS2o, Zero, Zeroo, BusB, BusBo, Imm, Result, PCTarget, Dout, Immo, Resulto, PCTargeto, Douto
  or or_2 (or_2_out, \转发检测_1_busafw [0], \转发检测_1_busafw [1]);
  Counter #(.width(16), .max('hffff)) counter_7 (
    .count(and_8_out), .Q(\RS2转发次数 ), .clk(clk_t), .clr(ReSet));  // open: load, D, carry, preset, down
  and and_8 (and_8_out, ~Stop, and_9_out);  // AND_Gate
  or or_3 (or_3_out, ReSet, \跳转检测_1_pcsrc );
  \阻塞检测  \u_阻塞检测_1  (
    .EX_MemtoReg(\流水段寄存器_2_memtorego ), .EX_rd(\流水段寄存器_2_rdo ), .Stall(\阻塞检测_1_stall ),
    .IF_opcode(idu_1_opcode), .IF_rs1(idu_1_rs1), .IF_rs2(idu_1_rs2));
  \控制器  \u_控制器_1  (
    .opcode(idu_1_opcode), .ExtOp(\控制器_1_extop ), .RegWr(\控制器_1_regwr ), .BandJ(\控制器_1_bandj ),
    .funct3(idu_1_funct3), .ALUASrc(\控制器_1_aluasrc ), .ALUBSrc(\控制器_1_alubsrc ), .ALUctr(\控制器_1_aluctr ),
    .funct7(idu_1_funct7), .MemtoReg(\控制器_1_memtoreg ), .MemOp(\控制器_1_memop ), .MemWr(\控制器_1_memwr ),
    .Halt(\控制器_1_halt ), .Stall(\阻塞检测_1_stall ));
  IDU idu_1 (
    .OpCode(idu_1_opcode), .RegWr(\流水段寄存器_4_regwro ), .Imm(idu_1_imm), .Funct3(idu_1_funct3),
    .Funct7(idu_1_funct7), .CLK(clk_t), .IR(\流水段寄存器_1_iro ), .BusW(WB_BusW), .BusA(idu_1_busa),
    .BusB(idu_1_busb), .ExtOp(\控制器_1_extop ), .Rd(idu_1_rd), .Rs1(idu_1_rs1), .Rs2(idu_1_rs2),
    .WB_Rd(\流水段寄存器_4_rdo ));
  and and_9 (and_9_out, or_4_out, nor_2_out);
  or or_4 (or_4_out, \转发检测_1_busbfw [0], \转发检测_1_busbfw [1]);
  nor nor_2 (nor_2_out, \流水段寄存器_2_alubsrco [0], \流水段寄存器_2_alubsrco [1]);
  not not_3 (not_3_out, and_7_out);
  \流水段寄存器  \u_流水段寄存器_2  (
    .ALUctr(\控制器_1_aluctr ), .ALUctro(\流水段寄存器_2_aluctro ), .CLR(or_3_out), .ALUASrc(\控制器_1_aluasrc ),
    .ALUASrco(\流水段寄存器_2_aluasrco ), .CLK(clk_t), .ALUBSrc(\控制器_1_alubsrc ), .ALUBSrco(\流水段寄存器_2_alubsrco ),
    .WE(not_3_out), .Halt(\控制器_1_halt ), .Halto(\流水段寄存器_2_halto ), .BandJ(\控制器_1_bandj ),
    .BandJo(\流水段寄存器_2_bandjo ), .PC(ID_PC), .MemOp(\控制器_1_memop ), .PCo(EX_PC), .MemOpo(\流水段寄存器_2_memopo ),
    .MemWr(\控制器_1_memwr ), .MemWro(\流水段寄存器_2_memwro ), .RegWr(\控制器_1_regwr ), .RegWro(\流水段寄存器_2_regwro ),
    .IR(\流水段寄存器_1_iro ), .MemtoReg(\控制器_1_memtoreg ), .IRo(\流水段寄存器_2_iro ), .MemtoRego(\流水段寄存器_2_memtorego ),
    .RD(idu_1_rd), .RDo(\流水段寄存器_2_rdo ), .BusA(idu_1_busa), .BusAo(\流水段寄存器_2_busao ), .RS1(idu_1_rs1),
    .RS1o(\流水段寄存器_2_rs1o ), .RS2(idu_1_rs2), .RS2o(\流水段寄存器_2_rs2o ), .BusB(idu_1_busb),
    .BusBo(\流水段寄存器_2_busbo ), .Imm(idu_1_imm), .Immo(\流水段寄存器_2_immo ));  // open: Zero, Zeroo, Result, PCTarget, Dout, Resulto, PCTargeto, Douto
  Multiplexer #(.select(2), .width(32), .enable("false")) multiplexer_1 (
    .in0(\流水段寄存器_2_busao ), .in1({\流水段寄存器_3_resulto_2 , \流水段寄存器_3_resulto }), .in2(WB_BusW),
    .out(multiplexer_1_out), .sel(\转发检测_1_busafw ));  // open: in3
  Multiplexer #(.select(2), .width(32), .enable("false")) multiplexer_2 (
    .in0(\流水段寄存器_2_busbo ), .in1({\流水段寄存器_3_resulto_2 , \流水段寄存器_3_resulto }), .in2(WB_BusW),
    .out(multiplexer_2_out), .sel(\转发检测_1_busbfw ));  // open: in3
  Comparator #(.width(3)) comparator_2 (.a(\流水段寄存器_2_bandjo ), .b(3'b010), .eq(comparator_2_eq));  // open: gt, lt
  Multiplexer #(.select(2), .width(32), .enable("false")) multiplexer_3 (
    .in0(multiplexer_2_out), .in1(32'h4), .in2(\流水段寄存器_2_immo ), .out(multiplexer_3_out),
    .sel(\流水段寄存器_2_alubsrco ));  // open: in3
  // Probe on IF_PC
  // Probe on ID_PC
  // Probe on EX_PC
  // Probe on M_PC
  // Probe on WB_PC
  \转发检测  \u_转发检测_1  (
    .EX_rs1(\流水段寄存器_2_rs1o ), .M_RegWr(\流水段寄存器_3_regwro ), .EX_rs2(\流水段寄存器_2_rs2o ), .M_rd(\流水段寄存器_3_rdo ),
    .WB_RegWr(\流水段寄存器_4_regwro ), .WB_rd(\流水段寄存器_4_rdo ), .BusAFW(\转发检测_1_busafw ), .BusBFW(\转发检测_1_busbfw ));
  Multiplexer #(.width(32), .enable("false")) multiplexer_4 (
    .in0(EX_PC), .in1(multiplexer_1_out), .out(multiplexer_4_out), .sel(comparator_2_eq));
  Adder #(.width(32)) adder_1 (.a(multiplexer_4_out), .b(\流水段寄存器_2_immo ), .out(adder_1_out));  // open: cin, cout
  Multiplexer #(.width(32), .enable("false")) multiplexer_5 (
    .in0(multiplexer_1_out), .in1(EX_PC), .out(multiplexer_5_out), .sel(\流水段寄存器_2_aluasrco ));
  ALU alu_1 (.A(multiplexer_5_out), .B(multiplexer_3_out), .ALUctr(\流水段寄存器_2_aluctro ), .S(alu_1_s), .Zero(alu_1_zero));
  not not_4 (not_4_out, and_7_out);
  or or_5 (or_5_out, ReSet, \跳转检测_1_pcsrc );
  \流水段寄存器  \u_流水段寄存器_3  (
    .ALUctr(\流水段寄存器_2_aluctro ), .ALUctro(\流水段寄存器_3_aluctro ), .CLR(or_5_out), .ALUASrc(\流水段寄存器_2_aluasrco ),
    .ALUASrco(\流水段寄存器_3_aluasrco ), .CLK(clk_t), .ALUBSrc(\流水段寄存器_2_alubsrco ),
    .ALUBSrco(\流水段寄存器_3_alubsrco ), .WE(not_4_out), .Halt(\流水段寄存器_2_halto ), .Halto(\流水段寄存器_3_halto ),
    .BandJ(\流水段寄存器_2_bandjo ), .BandJo(\流水段寄存器_3_bandjo ), .PC(EX_PC), .MemOp(\流水段寄存器_2_memopo ), .PCo(M_PC),
    .MemOpo(\流水段寄存器_3_memopo ), .MemWr(\流水段寄存器_2_memwro ), .MemWro(\流水段寄存器_3_memwro ),
    .RegWr(\流水段寄存器_2_regwro ), .RegWro(\流水段寄存器_3_regwro ), .IR(\流水段寄存器_2_iro ),
    .MemtoReg(\流水段寄存器_2_memtorego ), .IRo(\流水段寄存器_3_iro ), .MemtoRego(\流水段寄存器_3_memtorego ),
    .RD(\流水段寄存器_2_rdo ), .RDo(\流水段寄存器_3_rdo ), .BusA(multiplexer_1_out), .BusAo(\流水段寄存器_3_busao ),
    .RS1(\流水段寄存器_2_rs1o ), .RS1o(\流水段寄存器_3_rs1o ), .RS2(\流水段寄存器_2_rs2o ), .RS2o(\流水段寄存器_3_rs2o ),
    .Zero(alu_1_zero), .Zeroo(\流水段寄存器_3_zeroo ), .BusB(multiplexer_2_out), .BusBo(\流水段寄存器_3_busbo ),
    .Imm(\流水段寄存器_2_immo ), .Result(alu_1_s), .PCTarget(adder_1_out), .Immo(\流水段寄存器_3_immo ),
    .Resulto({\流水段寄存器_3_resulto_2 , \流水段寄存器_3_resulto }), .PCTargeto(\流水段寄存器_3_pctargeto ));  // open: Dout, Douto
  // Probe on Cycles
  // Probe on \阻塞次数 
  // Probe on \冲刷次数 
  // Probe on \跳转指令数 
  // Probe on \分支指令数 
  \跳转检测  \u_跳转检测_1  (
    .M_BandJ(\流水段寄存器_3_bandjo ), .PCsrc(\跳转检测_1_pcsrc ), .M_Zero(\流水段寄存器_3_zeroo ),
    .M_Result0(\流水段寄存器_3_resulto [0]));
  // Probe on \RS1转发次数 
  // Probe on \RS2转发次数 
  DataRAM dataram_1 (
    .Addr(\流水段寄存器_3_resulto ), .Din(\流水段寄存器_3_busbo ), .CLK(clk_t), .CLR(ReSet), .WE(\流水段寄存器_3_memwro ),
    .MemOp(\流水段寄存器_3_memopo ), .DataOut(dataram_1_dataout));  // open: AlignErr
  Comparator #(.width(3)) comparator_3 (.a(\流水段寄存器_3_bandjo ), .b(3'b001), .eq(comparator_3_eq));  // open: gt, lt
  Comparator #(.width(3)) comparator_4 (.a(\流水段寄存器_3_bandjo ), .b(3'b010), .eq(comparator_4_eq));  // open: gt, lt
  or or_6 (or_6_out, comparator_4_eq, comparator_3_eq);
  Register #(.width(1), .trigger("falling"), .Select("low")) register_1 (
    .D(halt), .en(not_5_out), .Q(Stop), .clk(clk_t), .clr(ReSet));
  not not_5 (not_5_out, Stop);
  not not_6 (not_6_out, and_7_out);
  \流水段寄存器  \u_流水段寄存器_4  (
    .ALUctr(\流水段寄存器_3_aluctro ), .CLR(ReSet), .ALUASrc(\流水段寄存器_3_aluasrco ), .CLK(clk_t),
    .ALUBSrc(\流水段寄存器_3_alubsrco ), .WE(not_6_out), .Halt(\流水段寄存器_3_halto ), .Halto(halt),
    .BandJ(\流水段寄存器_3_bandjo ), .PC(M_PC), .MemOp(\流水段寄存器_3_memopo ), .PCo(WB_PC), .MemWr(\流水段寄存器_3_memwro ),
    .RegWr(\流水段寄存器_3_regwro ), .RegWro(\流水段寄存器_4_regwro ), .IR(\流水段寄存器_3_iro ),
    .MemtoReg(\流水段寄存器_3_memtorego ), .IRo(WB_IR), .MemtoRego(\流水段寄存器_4_memtorego ), .RD(\流水段寄存器_3_rdo ),
    .RDo(\流水段寄存器_4_rdo ), .BusA(\流水段寄存器_3_busao ), .RS1(\流水段寄存器_3_rs1o ), .RS2(\流水段寄存器_3_rs2o ),
    .Zero(\流水段寄存器_3_zeroo ), .BusB(\流水段寄存器_3_busbo ), .Imm(\流水段寄存器_3_immo ),
    .Result({\流水段寄存器_3_resulto_2 , \流水段寄存器_3_resulto }), .PCTarget(\流水段寄存器_3_pctargeto ),
    .Dout(dataram_1_dataout), .Resulto(\流水段寄存器_4_resulto ), .Douto(\流水段寄存器_4_douto ));  // open: ALUctro, ALUASrco, ALUBSrco, BandJo, MemOpo, MemWro, BusAo, RS1o, RS2o, Zeroo, BusBo, Immo, PCTargeto
  Multiplexer #(.width(32), .enable("false")) multiplexer_6 (
    .in0(\流水段寄存器_4_resulto ), .in1(\流水段寄存器_4_douto ), .out(WB_BusW), .sel(\流水段寄存器_4_memtorego ));
  Hex_Digit_Display hex_digit_display_1 (.value(WB_IR[27:24]));  // open: dp
  Hex_Digit_Display hex_digit_display_2 (.value(WB_IR[31:28]));  // open: dp
  Hex_Digit_Display hex_digit_display_3 (.value(WB_IR[19:16]));  // open: dp
  Hex_Digit_Display hex_digit_display_4 (.value(WB_IR[23:20]));  // open: dp
  Hex_Digit_Display hex_digit_display_5 (.value(WB_IR[11:8]));  // open: dp
  Hex_Digit_Display hex_digit_display_6 (.value(WB_IR[15:12]));  // open: dp
  Hex_Digit_Display hex_digit_display_7 (.value(WB_IR[7:4]));  // open: dp
  Hex_Digit_Display hex_digit_display_8 (.value(WB_IR[3:0]));  // open: dp

  // Other names for the same wires on the sheet: BP_En = BPEn; 总周期数[15:0] = Cycles

  // Notes on the sheet:
  //   断点调试
  //   输入引脚
  //   contents of rom_1 (hex, n*v repeats v):
  //   80000037 7ff00013 10c0b3 100193 18101463 800000b7 ffff8137 208733 7fff83b7 200193 16771863 ff010b7
  //   ff008093 f0f0f137 f010113 20f7b3 f003b7 f038393 300193 14779663 100093 3f00113 209833 800003b7
  //   400193 12781a63 800000b7 e00113 4020d8b3 fffe03b7 500193 10789e63 800000b7 7ff0a913 100393 600193
  //   10791463 800000b7 7ff0b993 393 700193 e799a63 2097 f5808093 ee00113 208023 ff00113 2080a3 c000113
  //   208123 113 2081a3 fff00393 800193 108a03 a7a1e63 900193 103b7 fee38393 da83 a7a9463 a00193 209b03
  //   c000393 1509223 87b1a63 b00193 c103b7 fee38393 ab83 87b9063 c00193 c103b7 fee38393 8213 22c03
  //   1822223 422f83 67f9063 d00193 c97 10c8ce7 33 4c0006f 397 ff838393 47c9063 e00193 a00413 6513 106593
  //   100493 a58633 b00533 c005b3 148493 944463 fedff0ef c22423 c10537 fee50513 73 deade537 ead50513 73
  //   输出引脚
  //   请勿修改引脚名称、电路名称及电路封装外观
  //   为方便调试，需要输出流水线各段保存的PC值、时钟周期数、冒险处理次数、分支与跳转指令执行数等信息
  //   流水调试日志
  //   程序运行分析
  //   程序执行结束
  //   数码管输出
endmodule

module \跳转检测  (
  input  [2:0] M_BandJ,
  input  M_Zero,
  input  M_Result0,
  output PCsrc
);

  wire not_1_out, or_1_out;

  not not_1 (not_1_out, M_Zero);
  or or_1 (or_1_out, ~M_Result0, M_Zero);  // OR_Gate
  Multiplexer #(.select(3), .enable("false")) multiplexer_1 (
    .in0(1'b0), .in1(1'b1), .in2(1'b1), .in4(M_Zero), .in5(not_1_out), .in6(M_Result0), .in7(or_1_out),
    .out(PCsrc), .sel(M_BandJ));  // open: in3

  // Notes on the sheet:
  //   M_BandJ: pull=down
  //   M_Zero: pull=down
  //   输入信号
  //   请勿修改引脚名称、电路名称及电路封装外观
  //   不要修改控制信号的编码定义、引脚名称和在布局中的位置。
  //   输出信号
endmodule

module \控制器  (
  input  [6:0] opcode,
  input  [2:0] funct3,
  input  [6:0] funct7,
  input  Stall,
  output [2:0] ExtOp,
  output RegWr,
  output [2:0] BandJ,
  output ALUASrc,
  output [1:0] ALUBSrc,
  output [3:0] ALUctr,
  output MemtoReg,
  output [2:0] MemOp,
  output MemWr,
  output Halt
);

  wire and_1_out, B_beq___B_bgeu, comparator_10_eq, comparator_11_eq, I_addi___I_srai, I_lb___I_lhu, J_jal,
       J_jalr, or_1_out, or_4_out, or_6_out, or_8_out, or_9_out, or_12_out, R_add___R_and, S_sb___S_sw,
       U_auipc, U_lui;
  wire [1:0] or_2_out, or_5_out, or_11_out;
  wire [2:0] multiplexer_13_out, multiplexer_14_out, multiplexer_15_out, multiplexer_16_out;
  wire [3:0] multiplexer_2_out, multiplexer_3_out, multiplexer_4_out;
  wire [3:3] multiplexer_1_out;

  Comparator #(.width(7)) comparator_1 (.a(opcode), .b(7'b0110111), .eq(U_lui));  // open: gt, lt
  Comparator #(.width(7)) comparator_2 (.a(opcode), .b(7'b0010111), .eq(U_auipc));  // open: gt, lt
  Comparator #(.width(7)) comparator_3 (.a(opcode), .b(7'b0010011), .eq(I_addi___I_srai));  // open: gt, lt
  Comparator #(.width(7)) comparator_4 (.a(opcode), .b(7'b0110011), .eq(R_add___R_and));  // open: gt, lt
  Comparator #(.width(7)) comparator_5 (.a(opcode), .b(7'b1101111), .eq(J_jal));  // open: gt, lt
  Comparator #(.width(7)) comparator_6 (.a(opcode), .b(7'b1100111), .eq(J_jalr));  // open: gt, lt
  Comparator #(.width(7)) comparator_7 (.a(opcode), .b(7'b1100011), .eq(B_beq___B_bgeu));  // open: gt, lt
  Comparator #(.width(7)) comparator_8 (.a(opcode), .b(7'b0000011), .eq(I_lb___I_lhu));  // open: gt, lt
  Comparator #(.width(7)) comparator_9 (.a(opcode), .b(7'b0100011), .eq(S_sb___S_sw));  // open: gt, lt
  and and_1 (and_1_out, I_addi___I_srai, comparator_10_eq);
  Comparator #(.width(3), .mode("unsigned")) comparator_10 (
    .a(funct3), .b(3'b101), .eq(comparator_10_eq));  // open: gt, lt
  Multiplexer #(.enable("false")) multiplexer_1 (
    .in0(1'b0), .in1(funct7[5]), .out(multiplexer_1_out[3]), .sel(or_1_out));
  or or_1 (or_1_out, and_1_out, R_add___R_and);
  or or_2 (or_2_out[0], U_lui, U_auipc, B_beq___B_bgeu);
  or or_3 (or_2_out[1], B_beq___B_bgeu, S_sb___S_sw);
  or or_4 (or_4_out, J_jal, J_jalr, U_auipc);
  or or_5 (or_5_out[0], J_jal, J_jalr);
  or or_6 (or_6_out, U_lui, U_auipc, J_jalr, R_add___R_and, J_jal, I_addi___I_srai, I_lb___I_lhu);
  or or_7 (or_5_out[1], I_lb___I_lhu, U_lui, I_addi___I_srai, S_sb___S_sw, U_auipc);
  Multiplexer #(.width(4), .enable("false")) multiplexer_2 (
    .in0(4'b0000), .in1(4'b1111), .out(multiplexer_2_out), .sel(U_lui));
  Multiplexer #(.width(4), .enable("false")) multiplexer_3 (
    .in0({3'b001, funct3[1]}), .in1({multiplexer_1_out[3], funct3}), .out(multiplexer_3_out), .sel(or_8_out));
  Comparator #(.width(7)) comparator_11 (.a(opcode), .b(7'b1110011), .eq(comparator_11_eq));  // open: gt, lt
  or or_8 (or_8_out, I_addi___I_srai, R_add___R_and);
  or or_9 (or_9_out, or_8_out, B_beq___B_bgeu);
  Multiplexer #(.width(4), .enable("false")) multiplexer_4 (
    .in0(multiplexer_2_out), .in1(multiplexer_3_out), .out(multiplexer_4_out), .sel(or_9_out));
  Multiplexer #(.width(3), .enable("false")) multiplexer_5 (
    .in0({J_jal, or_2_out}), .in1(3'b000), .out(ExtOp), .sel(Stall));
  Multiplexer #(.enable("false")) multiplexer_6 (.in0(or_4_out), .in1(1'b0), .out(ALUASrc), .sel(Stall));
  Multiplexer #(.enable("false")) multiplexer_7 (.in0(or_6_out), .in1(1'b0), .out(RegWr), .sel(Stall));
  Multiplexer #(.width(2), .enable("false")) multiplexer_8 (.in0(or_5_out), .in1(2'b00), .out(ALUBSrc), .sel(Stall));
  Multiplexer #(.enable("false")) multiplexer_9 (.in0(I_lb___I_lhu), .in1(1'b0), .out(MemtoReg), .sel(Stall));
  Multiplexer #(.width(4), .enable("false")) multiplexer_10 (
    .in0(multiplexer_4_out), .in1(4'b0000), .out(ALUctr), .sel(Stall));
  Multiplexer #(.enable("false")) multiplexer_11 (.in0(comparator_11_eq), .in1(1'b0), .out(Halt), .sel(Stall));
  Multiplexer #(.enable("false")) multiplexer_12 (.in0(S_sb___S_sw), .in1(1'b0), .out(MemWr), .sel(Stall));
  Multiplexer #(.select(3), .width(3), .enable("false")) multiplexer_13 (
    .in0(3'b100), .in1(3'b101), .in4(3'b110), .in5(3'b111), .in6(3'b110), .in7(3'b111),
    .out(multiplexer_13_out), .sel(funct3));  // open: in2, in3
  or or_10 (or_11_out[1], J_jal, J_jalr);
  or or_11 (or_11_out[0], J_jalr, B_beq___B_bgeu);
  Multiplexer #(.select(3), .width(3), .enable("false")) multiplexer_14 (
    .in0(3'b101), .in1(3'b110), .in2(3'b000), .in3(3'b000), .in4(3'b001), .in5(3'b010),
    .out(multiplexer_14_out), .sel(funct3));  // open: in6, in7
  or or_12 (or_12_out, S_sb___S_sw, I_lb___I_lhu);
  Multiplexer #(.select(2), .width(3), .enable("false")) multiplexer_15 (
    .in0(3'b000), .in1(multiplexer_13_out), .in2(3'b001), .in3(3'b010), .out(multiplexer_15_out),
    .sel(or_11_out));
  Multiplexer #(.width(3), .enable("false")) multiplexer_16 (
    .in0(3'b000), .in1(multiplexer_14_out), .out(multiplexer_16_out), .sel(or_12_out));
  Multiplexer #(.width(3), .enable("false")) multiplexer_17 (
    .in0(multiplexer_15_out), .in1(3'b000), .out(BandJ), .sel(Stall));
  Multiplexer #(.width(3), .enable("false")) multiplexer_18 (
    .in0(multiplexer_16_out), .in1(3'b000), .out(MemOp), .sel(Stall));

  // Notes on the sheet:
  //   输入引脚
  //   请勿修改引脚名称、电路名称及电路封装外观
  //   提示：根据指令种类，把7位指令code用一位指令类型标志位来表示，再通过功能码来区分具体指令，生成控制信号。
  //   输出引脚
endmodule

module IFU (
  input  Reset,
  input  BPEn,
  input  PCSrc,
  input  Stall,
  input  [31:0] Initial_Address,
  input  [31:0] BP_PC,
  input  [31:0] PCTarget,
  input  CLK,
  input  halt,
  output [31:0] PC
);

  wire and_1_out, comparator_1_eq, or_1_out;
  wire [31:0] adder_1_out, multiplexer_1_out, multiplexer_2_out, multiplexer_3_out;

  Adder #(.width(32)) adder_1 (.a(PC), .b(32'h4), .out(adder_1_out));  // open: cin, cout
  or or_1 (or_1_out, and_1_out, halt, Stall);
  and and_1 (and_1_out, comparator_1_eq, BPEn);
  Comparator #(.width(32)) comparator_1 (.a(PC), .b(BP_PC), .eq(comparator_1_eq));  // open: gt, lt
  Multiplexer #(.width(32), .enable("false")) multiplexer_1 (
    .in0(adder_1_out), .in1(PC), .out(multiplexer_1_out), .sel(or_1_out));
  Multiplexer #(.width(32), .enable("false")) multiplexer_2 (
    .in0(multiplexer_1_out), .in1(PCTarget), .out(multiplexer_2_out), .sel(PCSrc));
  Multiplexer #(.width(32), .enable("false")) multiplexer_3 (
    .in0(multiplexer_2_out), .in1(Initial_Address), .out(multiplexer_3_out), .sel(Reset));
  Register #(.width(32), .Select("low")) register_1 (.D(multiplexer_3_out), .Q(PC), .clk(CLK));  // open: en, clr

  // Other names for the same wires on the sheet: BP_En = BPEn; Init_Addr[31:0] = Initial_Address

  // Notes on the sheet:
  //   PCSrc: pull=down
  //   Stall: pull=down
  //   PCTarget: pull=down
  //   断点调试
  //   输入信号
  //   请勿修改引脚名称、电路名称及电路封装外观
  //   指令存储器256KB，数据位为32位，地址位为16位。PC寄存器数据宽度32位，片选信号高电平有效
  //   输出信号
endmodule

module RegFile (
  input  [4:0] R1_num,
  input  [4:0] R2_num,
  input  [4:0] Write_Reg_num,
  input  [31:0] Din,
  input  Write_Enable,
  input  Clock,
  output [31:0] Reg1Out,
  output [31:0] Reg2Out
);

  wire and_2_out, and_3_out, and_4_out, and_5_out, and_6_out, and_7_out, and_8_out, and_9_out, and_10_out,
       and_11_out, and_12_out, and_13_out, and_14_out, and_15_out, and_16_out, and_17_out, and_18_out,
       and_19_out, and_20_out, and_21_out, and_22_out, and_23_out, and_24_out, and_25_out, and_26_out,
       and_27_out, and_28_out, and_29_out, and_30_out, and_31_out, and_32_out, decoder_1_out0,
       decoder_1_out1, decoder_1_out2, decoder_1_out3, decoder_1_out4, decoder_1_out5, decoder_1_out6,
       decoder_1_out7, decoder_1_out8, decoder_1_out9, decoder_1_out10, decoder_1_out11, decoder_1_out12,
       decoder_1_out13, decoder_1_out14, decoder_1_out15, decoder_1_out16, decoder_1_out17, decoder_1_out18,
       decoder_1_out19, decoder_1_out20, decoder_1_out21, decoder_1_out22, decoder_1_out23, decoder_1_out24,
       decoder_1_out25, decoder_1_out26, decoder_1_out27, decoder_1_out28, decoder_1_out29, decoder_1_out30,
       decoder_1_out31, not_1_out;
  wire [31:0] _0_q, _1_q, _2_q, _3_q, _4_q, _5_q, _6_q, _7_q, _8_q, _9_q, register_1_q, register_2_q,
       register_3_q, register_4_q, register_5_q, register_6_q, register_7_q, register_8_q, register_9_q,
       register_10_q, register_11_q, register_12_q, register_13_q, register_14_q, register_15_q,
       register_16_q, register_17_q, register_18_q, register_19_q, register_20_q, register_21_q,
       register_22_q;

  Decoder #(.select(5), .enable("false")) decoder_1 (
    .out0(decoder_1_out0), .out1(decoder_1_out1), .out2(decoder_1_out2), .out3(decoder_1_out3),
    .out4(decoder_1_out4), .out5(decoder_1_out5), .out6(decoder_1_out6), .out7(decoder_1_out7),
    .out8(decoder_1_out8), .out9(decoder_1_out9), .out10(decoder_1_out10), .out11(decoder_1_out11),
    .out12(decoder_1_out12), .out13(decoder_1_out13), .out14(decoder_1_out14), .out15(decoder_1_out15),
    .out16(decoder_1_out16), .out17(decoder_1_out17), .out18(decoder_1_out18), .out19(decoder_1_out19),
    .out20(decoder_1_out20), .out21(decoder_1_out21), .out22(decoder_1_out22), .out23(decoder_1_out23),
    .out24(decoder_1_out24), .out25(decoder_1_out25), .out26(decoder_1_out26), .out27(decoder_1_out27),
    .out28(decoder_1_out28), .out29(decoder_1_out29), .out30(decoder_1_out30), .out31(decoder_1_out31),
    .sel(Write_Reg_num));
  // AND_Gate and_1 has open pins: in0=Write_Enable, in1=decoder_1_out0, out=open
  and and_2 (and_2_out, Write_Enable, decoder_1_out1);
  and and_3 (and_3_out, Write_Enable, decoder_1_out2);
  and and_4 (and_4_out, Write_Enable, decoder_1_out3);
  and and_5 (and_5_out, Write_Enable, decoder_1_out4);
  and and_6 (and_6_out, Write_Enable, decoder_1_out5);
  and and_7 (and_7_out, Write_Enable, decoder_1_out6);
  and and_8 (and_8_out, Write_Enable, decoder_1_out7);
  and and_9 (and_9_out, Write_Enable, decoder_1_out8);
  and and_10 (and_10_out, Write_Enable, decoder_1_out9);
  and and_11 (and_11_out, Write_Enable, decoder_1_out10);
  and and_12 (and_12_out, Write_Enable, decoder_1_out11);
  and and_13 (and_13_out, Write_Enable, decoder_1_out12);
  and and_14 (and_14_out, Write_Enable, decoder_1_out13);
  and and_15 (and_15_out, Write_Enable, decoder_1_out14);
  and and_16 (and_16_out, Write_Enable, decoder_1_out15);
  and and_17 (and_17_out, Write_Enable, decoder_1_out16);
  and and_18 (and_18_out, Write_Enable, decoder_1_out17);
  and and_19 (and_19_out, Write_Enable, decoder_1_out18);
  and and_20 (and_20_out, Write_Enable, decoder_1_out19);
  and and_21 (and_21_out, Write_Enable, decoder_1_out20);
  and and_22 (and_22_out, Write_Enable, decoder_1_out21);
  and and_23 (and_23_out, Write_Enable, decoder_1_out22);
  and and_24 (and_24_out, Write_Enable, decoder_1_out23);
  and and_25 (and_25_out, Write_Enable, decoder_1_out24);
  and and_26 (and_26_out, Write_Enable, decoder_1_out25);
  and and_27 (and_27_out, Write_Enable, decoder_1_out26);
  and and_28 (and_28_out, Write_Enable, decoder_1_out27);
  and and_29 (and_29_out, Write_Enable, decoder_1_out28);
  and and_30 (and_30_out, Write_Enable, decoder_1_out29);
  and and_31 (and_31_out, Write_Enable, decoder_1_out30);
  and and_32 (and_32_out, Write_Enable, decoder_1_out31);
  not not_1 (not_1_out, Clock);
  Register #(.width(32), .Select("low")) _0 (.D(Din), .en(1'b0), .Q(_0_q), .clr(1'b1));  // open: clk
  Register #(.width(32), .Select("low")) _1 (.D(Din), .en(and_2_out), .Q(_1_q), .clk(not_1_out));  // open: clr
  Register #(.width(32), .Select("low")) _2 (.D(Din), .en(and_3_out), .Q(_2_q), .clk(not_1_out));  // open: clr
  Register #(.width(32), .Select("low")) _3 (.D(Din), .en(and_4_out), .Q(_3_q), .clk(not_1_out));  // open: clr
  Register #(.width(32), .Select("low")) _4 (.D(Din), .en(and_5_out), .Q(_4_q), .clk(not_1_out));  // open: clr
  Register #(.width(32), .Select("low")) _5 (.D(Din), .en(and_6_out), .Q(_5_q), .clk(not_1_out));  // open: clr
  Register #(.width(32), .Select("low")) _6 (.D(Din), .en(and_7_out), .Q(_6_q), .clk(not_1_out));  // open: clr
  Register #(.width(32), .Select("low")) _7 (.D(Din), .en(and_8_out), .Q(_7_q), .clk(not_1_out));  // open: clr
  Register #(.width(32), .Select("low")) _8 (.D(Din), .en(and_9_out), .Q(_8_q), .clk(not_1_out));  // open: clr
  Register #(.width(32), .Select("low")) _9 (.D(Din), .en(and_10_out), .Q(_9_q), .clk(not_1_out));  // open: clr
  Register #(.width(32), .Select("low")) register_1 (
    .D(Din), .en(and_11_out), .Q(register_1_q), .clk(not_1_out));  // open: clr
  Register #(.width(32), .Select("low")) register_2 (
    .D(Din), .en(and_12_out), .Q(register_2_q), .clk(not_1_out));  // open: clr
  Register #(.width(32), .Select("low")) register_3 (
    .D(Din), .en(and_13_out), .Q(register_3_q), .clk(not_1_out));  // open: clr
  Register #(.width(32), .Select("low")) register_4 (
    .D(Din), .en(and_14_out), .Q(register_4_q), .clk(not_1_out));  // open: clr
  Register #(.width(32), .Select("low")) register_5 (
    .D(Din), .en(and_15_out), .Q(register_5_q), .clk(not_1_out));  // open: clr
  Register #(.width(32), .Select("low")) register_6 (
    .D(Din), .en(and_16_out), .Q(register_6_q), .clk(not_1_out));  // open: clr
  Register #(.width(32), .Select("low")) register_7 (
    .D(Din), .en(and_17_out), .Q(register_7_q), .clk(not_1_out));  // open: clr
  Register #(.width(32), .Select("low")) register_8 (
    .D(Din), .en(and_18_out), .Q(register_8_q), .clk(not_1_out));  // open: clr
  Register #(.width(32), .Select("low")) register_9 (
    .D(Din), .en(and_19_out), .Q(register_9_q), .clk(not_1_out));  // open: clr
  Register #(.width(32), .Select("low")) register_10 (
    .D(Din), .en(and_20_out), .Q(register_10_q), .clk(not_1_out));  // open: clr
  Register #(.width(32), .Select("low")) register_11 (
    .D(Din), .en(and_21_out), .Q(register_11_q), .clk(not_1_out));  // open: clr
  Register #(.width(32), .Select("low")) register_12 (
    .D(Din), .en(and_22_out), .Q(register_12_q), .clk(not_1_out));  // open: clr
  Register #(.width(32), .Select("low")) register_13 (
    .D(Din), .en(and_23_out), .Q(register_13_q), .clk(not_1_out));  // open: clr
  Register #(.width(32), .Select("low")) register_14 (
    .D(Din), .en(and_24_out), .Q(register_14_q), .clk(not_1_out));  // open: clr
  Register #(.width(32), .Select("low")) register_15 (
    .D(Din), .en(and_25_out), .Q(register_15_q), .clk(not_1_out));  // open: clr
  Register #(.width(32), .Select("low")) register_16 (
    .D(Din), .en(and_26_out), .Q(register_16_q), .clk(not_1_out));  // open: clr
  Register #(.width(32), .Select("low")) register_17 (
    .D(Din), .en(and_27_out), .Q(register_17_q), .clk(not_1_out));  // open: clr
  Register #(.width(32), .Select("low")) register_18 (
    .D(Din), .en(and_28_out), .Q(register_18_q), .clk(not_1_out));  // open: clr
  Register #(.width(32), .Select("low")) register_19 (
    .D(Din), .en(and_29_out), .Q(register_19_q), .clk(not_1_out));  // open: clr
  Register #(.width(32), .Select("low")) register_20 (
    .D(Din), .en(and_30_out), .Q(register_20_q), .clk(not_1_out));  // open: clr
  Register #(.width(32), .Select("low")) register_21 (
    .D(Din), .en(and_31_out), .Q(register_21_q), .clk(not_1_out));  // open: clr
  Register #(.width(32), .Select("low")) register_22 (
    .D(Din), .en(and_32_out), .Q(register_22_q), .clk(not_1_out));  // open: clr
  Multiplexer #(.select(5), .width(32), .enable("false")) multiplexer_1 (
    .in0(_0_q), .in1(_1_q), .in2(_2_q), .in3(_3_q), .in4(_4_q), .in5(_5_q), .in6(_6_q), .in7(_7_q),
    .in8(_8_q), .in9(_9_q), .in10(register_1_q), .in11(register_2_q), .in12(register_3_q),
    .in13(register_4_q), .in14(register_5_q), .in15(register_6_q), .in16(register_7_q), .in17(register_8_q),
    .in18(register_9_q), .in19(register_10_q), .in20(register_11_q), .in21(register_12_q),
    .in22(register_13_q), .in23(register_14_q), .in24(register_15_q), .in25(register_16_q),
    .in26(register_17_q), .in27(register_18_q), .in28(register_19_q), .in29(register_20_q),
    .in30(register_21_q), .in31(register_22_q), .out(Reg1Out), .sel(R1_num));
  Multiplexer #(.select(5), .width(32), .enable("false")) multiplexer_2 (
    .in0(_0_q), .in1(_1_q), .in2(_2_q), .in3(_3_q), .in4(_4_q), .in5(_5_q), .in6(_6_q), .in7(_7_q),
    .in8(_8_q), .in9(_9_q), .in10(register_1_q), .in11(register_2_q), .in12(register_3_q),
    .in13(register_4_q), .in14(register_5_q), .in15(register_6_q), .in16(register_7_q), .in17(register_8_q),
    .in18(register_9_q), .in19(register_10_q), .in20(register_11_q), .in21(register_12_q),
    .in22(register_13_q), .in23(register_14_q), .in24(register_15_q), .in25(register_16_q),
    .in26(register_17_q), .in27(register_18_q), .in28(register_19_q), .in29(register_20_q),
    .in30(register_21_q), .in31(register_22_q), .out(Reg2Out), .sel(R2_num));

  // Other names for the same wires on the sheet: CLK = Clock; RA[4:0] = R1_num; RB[4:0] = R2_num; RDA[31:0] = Reg1Out;
  //   RDB[31:0] = Reg2Out; RW[4:0] = Write_Reg_num; WE = Write_Enable

  // Notes on the sheet:
  //   输入引脚
  //   请勿修改引脚名称、电路名称及电路封装外观
  //   提示：使用译码器、多路选择器和32位寄存器及逻辑门实现寄存器堆，禁止直接使用存储器组件。
  //   输出引脚
endmodule

module IDU (
  input  [2:0] ExtOp,
  input  RegWr,
  input  [4:0] WB_Rd,
  input  [31:0] IR,
  input  [31:0] BusW,
  input  CLK,
  output [6:0] OpCode,
  output [2:0] Funct3,
  output [6:0] Funct7,
  output [31:0] Imm,
  output [31:0] BusA,
  output [31:0] BusB,
  output [4:0] Rd,
  output [4:0] Rs1,
  output [4:0] Rs2
);

  \立即数扩展器  \u_立即数扩展器_1  (.Instr(IR), .Extop(ExtOp), .imm(Imm));
  RegFile regfile_1 (
    .R1_num(IR[19:15]), .R2_num(IR[24:20]), .Write_Reg_num(WB_Rd), .Write_Enable(RegWr), .Clock(CLK),
    .Din(BusW), .Reg1Out(BusA), .Reg2Out(BusB));

  assign Funct3 = IR[14:12];
  assign Funct7 = IR[31:25];
  assign OpCode = IR[6:0];
  assign Rd = IR[11:7];
  assign Rs1 = IR[19:15];
  assign Rs2 = IR[24:20];

  // Other names for the same wires on the sheet: op[6:0] = IR[6:0]

  // Notes on the sheet:
  //   RegWr: pull=down
  //   ExtOp: pull=down
  //   WB_Rd: pull=down
  //   BusW: pull=down
  //   输入信号
  //   为了后续实验中的引用，不要修改ExtOP编码定义。
  //   请勿修改引脚名称、电路名称及电路封装外观
  //   修改寄存器堆电路设计，0号寄存器始终为0。
  //   输出信号
endmodule

module \立即数扩展器  (
  input  [31:0] Instr,
  input  [2:0] Extop,
  output [31:0] imm
);

  wire [11:0] bit_extender_4_out;
  wire [19:0] bit_extender_3_out;
  wire [31:0] bit_extender_1_out, bit_extender_2_out;

  assign bit_extender_1_out = {{20{Instr[31]}}, Instr[31:20]};  // Bit_Extender bit_extender_1
  assign bit_extender_2_out = {{20{Instr[31]}}, {Instr[31:25], Instr[11:7]}};  // Bit_Extender bit_extender_2
  assign bit_extender_3_out = {{19{Instr[31]}}, Instr[31]};  // Bit_Extender bit_extender_3
  assign bit_extender_4_out = {{11{Instr[31]}}, Instr[31]};  // Bit_Extender bit_extender_4
  Multiplexer #(.select(3), .width(32), .enable("false")) multiplexer_1 (
    .in0(bit_extender_1_out), .in1({Instr[31:12], {12{1'b0}}}), .in2(bit_extender_2_out),
    .in3({bit_extender_3_out, Instr[7], Instr[30:25], Instr[11:8], 1'b0}),
    .in4({bit_extender_4_out, Instr[19:12], Instr[20], Instr[30:21], 1'b0}), .out(imm), .sel(Extop));  // open: in5, in6, in7

  // Notes on the sheet:
  //   Instr: pull=down
  //   Extop: pull=down
  //   输入引脚
  //   输出引脚
endmodule

module DataRAM (
  input  CLK,
  input  CLR,
  input  WE,
  input  [2:0] MemOp,
  input  [17:0] Addr,
  input  [31:0] Din,
  output AlignErr,
  output [31:0] DataOut
);

  wire and_1_out, and_2_out, and_3_out, and_4_out, and_5_out, and_6_out, and_7_out, and_8_out, and_9_out,
       and_10_out, and_11_out, and_12_out, and_13_out, and_14_out, not_1_out;
  wire [3:0] SEL;
  wire [7:0] IN0, IN1, IN2, IN3, OUT0, OUT1, OUT2, OUT3;
  wire [31:0] bit_extender_1_out, bit_extender_2_out, bit_extender_3_out, bit_extender_4_out,
       bit_extender_5_out, bit_extender_6_out, bit_extender_7_out, bit_extender_8_out, bit_extender_9_out,
       bit_extender_10_out, bit_extender_11_out, bit_extender_12_out, multiplexer_1_out, multiplexer_2_out,
       multiplexer_3_out, multiplexer_4_out, multiplexer_5_out, multiplexer_6_out;

  and and_1 (and_1_out, ~Addr[0], ~Addr[1]);  // AND_Gate
  and and_2 (and_2_out, Addr[0], ~Addr[1]);  // AND_Gate
  and and_3 (and_3_out, ~Addr[0], Addr[1]);  // AND_Gate
  and and_4 (and_4_out, Addr[0], Addr[1]);
  and and_5 (and_5_out, ~MemOp[0], ~MemOp[1], ~MemOp[2]);  // AND_Gate
  and and_6 (and_6_out, MemOp[0], ~MemOp[1]);  // AND_Gate
  and and_7 (and_7_out, ~MemOp[0], MemOp[1]);  // AND_Gate
  not not_1 (not_1_out, MemOp[2]);
  assign bit_extender_1_out = {{24{1'b0}}, OUT0};  // Bit_Extender bit_extender_1
  assign bit_extender_2_out = {{24{1'b0}}, OUT1};  // Bit_Extender bit_extender_2
  assign bit_extender_3_out = {{24{1'b0}}, OUT2};  // Bit_Extender bit_extender_3
  assign bit_extender_4_out = {{24{1'b0}}, OUT3};  // Bit_Extender bit_extender_4
  assign bit_extender_5_out = {{16{1'b0}}, {OUT1, OUT0}};  // Bit_Extender bit_extender_5
  assign bit_extender_6_out = {{16{1'b0}}, {OUT3, OUT2}};  // Bit_Extender bit_extender_6
  RAM #(.addrWidth(16), .bus("separate"), .Select("high"), .simpleMode("false")) ram_1 (
    .addr(Addr[17:2]), .din(IN3), .data(OUT3), .str(WE), .sel(SEL[3]), .clk(CLK), .clr(CLR));  // open: ld
  and and_8 (and_8_out, and_5_out, and_1_out);
  and and_9 (and_9_out, and_6_out, and_1_out);
  and and_10 (and_10_out, and_6_out, and_2_out);
  and and_11 (and_11_out, and_6_out, and_3_out);
  and and_12 (and_12_out, and_6_out, and_4_out);
  and and_13 (and_13_out, and_7_out, and_1_out);
  and and_14 (and_14_out, and_7_out, and_3_out);
  assign bit_extender_7_out = {{24{OUT0[7]}}, OUT0};  // Bit_Extender bit_extender_7
  assign bit_extender_8_out = {{24{OUT1[7]}}, OUT1};  // Bit_Extender bit_extender_8
  assign bit_extender_9_out = {{24{OUT2[7]}}, OUT2};  // Bit_Extender bit_extender_9
  assign bit_extender_10_out = {{24{OUT3[7]}}, OUT3};  // Bit_Extender bit_extender_10
  assign bit_extender_11_out = {{16{OUT1[7]}}, {OUT1, OUT0}};  // Bit_Extender bit_extender_11
  assign bit_extender_12_out = {{16{OUT3[7]}}, {OUT3, OUT2}};  // Bit_Extender bit_extender_12
  Multiplexer #(.width(32), .enable("false")) multiplexer_1 (
    .in0(bit_extender_7_out), .in1(bit_extender_1_out), .out(multiplexer_1_out), .sel(not_1_out));
  Multiplexer #(.width(32), .enable("false")) multiplexer_2 (
    .in0(bit_extender_8_out), .in1(bit_extender_2_out), .out(multiplexer_2_out), .sel(not_1_out));
  Multiplexer #(.width(32), .enable("false")) multiplexer_3 (
    .in0(bit_extender_9_out), .in1(bit_extender_3_out), .out(multiplexer_3_out), .sel(not_1_out));
  Multiplexer #(.width(32), .enable("false")) multiplexer_4 (
    .in0(bit_extender_10_out), .in1(bit_extender_4_out), .out(multiplexer_4_out), .sel(not_1_out));
  Multiplexer #(.width(32), .enable("false")) multiplexer_5 (
    .in0(bit_extender_11_out), .in1(bit_extender_5_out), .out(multiplexer_5_out), .sel(not_1_out));
  Multiplexer #(.width(32), .enable("false")) multiplexer_6 (
    .in0(bit_extender_12_out), .in1(bit_extender_6_out), .out(multiplexer_6_out), .sel(not_1_out));
  or or_1 (SEL[0], and_8_out, and_13_out, and_9_out);
  or or_2 (SEL[1], and_8_out, and_13_out, and_10_out);
  or or_3 (SEL[2], and_8_out, and_14_out, and_11_out);
  or or_4 (SEL[3], and_8_out, and_14_out, and_12_out);
  nor nor_1 (AlignErr, and_8_out, and_14_out, and_9_out, and_10_out, and_11_out, and_12_out, and_13_out);
  Multiplexer #(.select(4), .width(32), .enable("false")) multiplexer_7 (
    .in1(multiplexer_1_out), .in2(multiplexer_2_out), .in3(multiplexer_5_out), .in4(multiplexer_3_out),
    .in8(multiplexer_4_out), .in12(multiplexer_6_out), .in15({OUT3, OUT2, OUT1, OUT0}), .out(DataOut),
    .sel(SEL));  // open: in0, in5, in6, in7, in9, in10, in11, in13, in14
  RAM #(.addrWidth(16), .bus("separate"), .Select("high"), .simpleMode("false")) ram_2 (
    .addr(Addr[17:2]), .din(IN2), .data(OUT2), .str(WE), .sel(SEL[2]), .clk(CLK), .clr(CLR));  // open: ld
  RAM #(.addrWidth(16), .bus("separate"), .Select("high"), .simpleMode("false")) ram_3 (
    .addr(Addr[17:2]), .din(IN1), .data(OUT1), .str(WE), .sel(SEL[1]), .clk(CLK), .clr(CLR));  // open: ld
  Multiplexer #(.select(4), .width(8), .enable("false")) multiplexer_8 (
    .in1(Din[7:0]), .in3(Din[7:0]), .in15(Din[7:0]), .out(IN0), .sel(SEL));  // open: in0, in2, in4, in5, in6, in7, in8, in9, in10, in11, in12, in13, in14
  Multiplexer #(.select(4), .width(8), .enable("false")) multiplexer_9 (
    .in2(Din[7:0]), .in3(Din[15:8]), .in15(Din[15:8]), .out(IN1), .sel(SEL));  // open: in0, in1, in4, in5, in6, in7, in8, in9, in10, in11, in12, in13, in14
  Multiplexer #(.select(4), .width(8), .enable("false")) multiplexer_10 (
    .in4(Din[7:0]), .in12(Din[7:0]), .in15(Din[23:16]), .out(IN2), .sel(SEL));  // open: in0, in1, in2, in3, in5, in6, in7, in8, in9, in10, in11, in13, in14
  Multiplexer #(.select(4), .width(8), .enable("false")) multiplexer_11 (
    .in8(Din[7:0]), .in12(Din[15:8]), .in15(Din[31:24]), .out(IN3), .sel(SEL));  // open: in0, in1, in2, in3, in4, in5, in6, in7, in9, in10, in11, in13, in14
  RAM #(.addrWidth(16), .bus("separate"), .Select("high"), .simpleMode("false")) ram_4 (
    .addr(Addr[17:2]), .din(IN0), .data(OUT0), .str(WE), .sel(SEL[0]), .clk(CLK), .clr(CLR));  // open: ld

  // Other names for the same wires on the sheet: Dout[31:0] = DataOut

  // Notes on the sheet:
  //   输入引脚
  //   请勿修改引脚名称、电路名称及电路封装外观
  //   为了后续实验中的引用，不要修改MemOp的编码定义、引脚名称和在布局中的位置。
  //   32位数据存储器，按字节分4片存储，可按照字节、半字和字进行存储；读取字节或半字时，支持0扩展和符号位扩展。
  //   输出引脚
endmodule

module ALU (
  input  [3:0] ALUctr,
  input  [31:0] A,
  input  [31:0] B,
  output Zero,
  output [31:0] S
);

  wire adder32_1_cf, adder32_1_of, adder32_1_sf, aluctrl_1_alctr, aluctrl_1_sftctr, aluctrl_1_sigctr,
       aluctrl_1_subctr, multiplexer_2_out, xor_3_out;
  wire [2:0] aluctrl_1_opctr;
  wire [31:0] adder32_1_s, and_1_out, bit_extender_1_out, bit_extender_2_out, or_1_out, shifter32_1_dataout,
       xor_1_out, xor_2_out;

  assign bit_extender_1_out = {{31{aluctrl_1_subctr}}, aluctrl_1_subctr};  // Bit_Extender bit_extender_1
  assign and_1_out = A & B;  // AND_Gate and_1, 32 bits wide
  assign or_1_out = A | B;  // OR_Gate or_1, 32 bits wide
  Adder32 adder32_1 (
    .CF(adder32_1_cf), .OF(adder32_1_of), .SF(adder32_1_sf), .ZF(Zero), .X(A), .Y(xor_1_out),
    .Cin(aluctrl_1_subctr), .S(adder32_1_s));  // open: Cout
  assign xor_1_out = B ^ bit_extender_1_out;  // XOR_Gate xor_1, 32 bits wide
  assign xor_2_out = A ^ B;  // XOR_Gate xor_2, 32 bits wide
  Shifter32 shifter32_1 (
    .DataIn(A), .shamt(B[4:0]), .L_R(aluctrl_1_sftctr), .A_L(aluctrl_1_alctr), .DataOut(shifter32_1_dataout));
  xor xor_3 (xor_3_out, adder32_1_of, adder32_1_sf);
  assign bit_extender_2_out = {{31{1'b0}}, multiplexer_2_out};  // Bit_Extender bit_extender_2
  Multiplexer #(.select(3), .width(32), .enable("false")) multiplexer_1 (
    .in0(adder32_1_s), .in1(and_1_out), .in2(or_1_out), .in3(xor_2_out), .in4(shifter32_1_dataout), .in5(B),
    .in6(bit_extender_2_out), .out(S), .sel(aluctrl_1_opctr));  // open: in7
  Multiplexer #(.enable("false")) multiplexer_2 (
    .in0(adder32_1_cf), .in1(xor_3_out), .out(multiplexer_2_out), .sel(aluctrl_1_sigctr));
  ALUctrl aluctrl_1 (
    .SUBctr(aluctrl_1_subctr), .SFTctr(aluctrl_1_sftctr), .SIGctr(aluctrl_1_sigctr), .ALctr(aluctrl_1_alctr),
    .OPctr(aluctrl_1_opctr), .ALUctr(ALUctr));
  // Probe on A
  // Probe on B
  // Probe on S

  // Other names for the same wires on the sheet: Result[31:0] = S

  // Notes on the sheet:
  //   B: pull=down
  //   A: pull=down
  //   ALUctr: pull=down
  //   输入引脚
  //   请勿修改引脚名称、电路名称及电路封装外观
  //   提示：使用32位并行加法器子电路、桶形移位器、ALU控制子电路实现32位ALU
  //   功能说明:32位ALU，输入32位操作数A、B，4位控制信号ALUctr，输出32位结果Reseult和1位Zero标志位
  //   输出引脚
  //   操作数和结果
endmodule

module ALUctrl (
  input  [3:0] ALUctr,
  output SUBctr,
  output SFTctr,
  output SIGctr,
  output ALctr,
  output [2:0] OPctr
);

  wire and_1_out, and_2_out, and_6_out, and_7_out, and_8_out, and_9_out, and_10_out, and_11_out;

  and and_1 (and_1_out, ~ALUctr[3], ~ALUctr[2], ALUctr[1]);  // AND_Gate
  or or_1 (SUBctr, and_1_out, and_2_out);
  and and_2 (and_2_out, ALUctr[3], ~ALUctr[2], ~ALUctr[1], ~ALUctr[0]);  // AND_Gate
  and and_3 (SIGctr, ~ALUctr[3], ~ALUctr[2], ALUctr[1], ~ALUctr[0]);  // AND_Gate
  and and_4 (ALctr, ALUctr[3], ALUctr[2], ~ALUctr[1], ALUctr[0]);  // AND_Gate
  and and_5 (SFTctr, ~ALUctr[3], ~ALUctr[2], ~ALUctr[1], ALUctr[0]);  // AND_Gate
  and and_6 (and_6_out, ~ALUctr[3], ~ALUctr[1], ALUctr[0]);  // AND_Gate
  and and_7 (and_7_out, ~ALUctr[3], ~ALUctr[2], ALUctr[1]);  // AND_Gate
  and and_8 (and_8_out, ALUctr[3], ALUctr[2], ALUctr[0]);
  and and_9 (and_9_out, ~ALUctr[3], ALUctr[2], ~ALUctr[0]);  // AND_Gate
  and and_10 (and_10_out, ALUctr[2], ALUctr[1], ALUctr[0]);
  and and_11 (and_11_out, ~ALUctr[3], ALUctr[2], ~ALUctr[1], ~ALUctr[0]);  // AND_Gate
  or or_2 (OPctr[2], and_6_out, and_7_out, and_8_out);
  or or_3 (OPctr[1], and_7_out, and_9_out);
  or or_4 (OPctr[0], and_10_out, and_11_out);

  // Other names for the same wires on the sheet: LRctr = SFTctr

  // Notes on the sheet:
  //   输入引脚
  //   输出引脚
endmodule

module Adder32 (
  input  Cin,
  input  [31:0] X,
  input  [31:0] Y,
  output CF,
  output Cout,
  output OF,
  output SF,
  output [31:0] S,
  output ZF
);

  wire adder16_2_c16, and_1_out, and_2_out, and_3_out, and_4_out;

  xor xor_1 (CF, Cout, Cin);
  Adder16 adder16_1 (.X(X[31:16]), .Y(Y[31:16]), .C0(adder16_2_c16), .S(S[31:16]), .C16(Cout));  // open: Pg, Gg
  Comparator #(.width(32)) comparator_1 (.a(S), .b({32{1'b0}}), .eq(ZF));  // open: gt, lt
  Adder16 adder16_2 (.X(X[15:0]), .Y(Y[15:0]), .C0(Cin), .S(S[15:0]), .C16(adder16_2_c16));  // open: Pg, Gg
  and and_1 (and_1_out, ~S[31], and_2_out);  // AND_Gate
  and and_2 (and_2_out, Y[31], X[31]);
  and and_3 (and_3_out, S[31], and_4_out);
  and and_4 (and_4_out, ~X[31], ~Y[31]);  // AND_Gate
  or or_1 (OF, and_1_out, and_3_out);
  // Probe on X
  // Probe on Y
  // Probe on S

  assign SF = S[31];

  // Notes on the sheet:
  //   X: pull=down
  //   Y: pull=down
  //   Cin: pull=down
  //   输入引脚区
  //   输出引脚区
  //   请勿修改引脚名称、电路名称及电路封装外观
  //   提示：使用16位并行加法器子电路实现32位快速加法器
  //   功能说明:32位Adder  S=X+Y，Cout为最高位进位位，Cin为进位输入， S为和，溢出OF、进位CF、零ZF、符号SF。
  //   +
  //   =
  //   无符号加法
endmodule

// 移位器
module Shifter32 (
  input  [4:0] shamt,
  input  L_R,
  input  A_L,
  input  [31:0] DataIn,
  output [31:0] DataOut
);

  wire [0:0] multiplexer_2_out;
  wire [1:0] multiplexer_4_out;
  wire [3:0] multiplexer_6_out;
  wire [7:0] multiplexer_8_out;
  wire [15:0] multiplexer_10_out;
  wire [31:0] multiplexer_3_out, multiplexer_5_out, multiplexer_7_out, multiplexer_9_out;
  wire [31:31] multiplexer_1_out;

  Multiplexer #(.enable("false")) multiplexer_1 (.in0(1'b0), .in1(DataIn[31]), .out(multiplexer_1_out[31]), .sel(A_L));
  Multiplexer #(.enable("false")) multiplexer_2 (.in0(1'b0), .in1(DataIn[31]), .out(multiplexer_2_out[0]), .sel(A_L));
  Multiplexer #(.select(2), .width(32), .enable("false")) multiplexer_3 (
    .in0(DataIn), .in1({multiplexer_1_out[31], DataIn[31:1]}), .in2(DataIn),
    .in3({DataIn[30:0], multiplexer_2_out[0]}), .out(multiplexer_3_out), .sel({L_R, shamt[0]}));
  Multiplexer #(.width(2), .enable("false")) multiplexer_4 (
    .in0(2'b00), .in1(multiplexer_3_out[31:30]), .out(multiplexer_4_out), .sel(A_L));
  Multiplexer #(.select(2), .width(32), .enable("false")) multiplexer_5 (
    .in0(multiplexer_3_out), .in1({{2{multiplexer_1_out[31]}}, multiplexer_3_out[31:2]}),
    .in2(multiplexer_3_out), .in3({multiplexer_3_out[29:0], multiplexer_4_out}), .out(multiplexer_5_out),
    .sel({L_R, shamt[1]}));
  Multiplexer #(.width(4), .enable("false")) multiplexer_6 (
    .in0(4'b0000), .in1(multiplexer_5_out[31:28]), .out(multiplexer_6_out), .sel(A_L));
  Multiplexer #(.select(2), .width(32), .enable("false")) multiplexer_7 (
    .in0(multiplexer_5_out), .in1({{4{multiplexer_1_out[31]}}, multiplexer_5_out[31:4]}),
    .in2(multiplexer_5_out), .in3({multiplexer_5_out[27:0], multiplexer_6_out}), .out(multiplexer_7_out),
    .sel({L_R, shamt[2]}));
  Multiplexer #(.width(8), .enable("false")) multiplexer_8 (
    .in0({8{1'b0}}), .in1(multiplexer_7_out[31:24]), .out(multiplexer_8_out), .sel(A_L));
  Multiplexer #(.select(2), .width(32), .enable("false")) multiplexer_9 (
    .in0(multiplexer_7_out), .in1({{8{multiplexer_1_out[31]}}, multiplexer_7_out[31:8]}),
    .in2(multiplexer_7_out), .in3({multiplexer_7_out[23:0], multiplexer_8_out}), .out(multiplexer_9_out),
    .sel({L_R, shamt[3]}));
  Multiplexer #(.width(16), .enable("false")) multiplexer_10 (
    .in0({16{1'b0}}), .in1(multiplexer_9_out[31:16]), .out(multiplexer_10_out), .sel(A_L));
  Multiplexer #(.select(2), .width(32), .enable("false")) multiplexer_11 (
    .in0(multiplexer_9_out), .in1({{16{multiplexer_1_out[31]}}, multiplexer_9_out[31:16]}),
    .in2(multiplexer_9_out), .in3({multiplexer_9_out[15:0], multiplexer_10_out}), .out(DataOut),
    .sel({L_R, shamt[4]}));

  // Other names for the same wires on the sheet: Din[31:0] = DataIn; Left_Right = L_R; Arth_Logic = A_L;
  //   Dout[31:0] = DataOut

  // Notes on the sheet:
  //   L/R,A/L: 00逻辑右移，01算术右移，10逻辑左移，11：循环左移
  //   输入引脚
  //   请勿修改引脚名称、电路名称及电路封装外观
  //   提示：使用多路选择器、逻辑门实现32位桶形移位器，禁止直接使用移位器组件。
  //   输出引脚
endmodule

module Adder16 (
  input  C0,
  input  [15:0] X,
  input  [15:0] Y,
  output C16,
  output Pg,
  output Gg,
  output [15:0] S
);

  wire cla4_1_gg, cla4_1_pg, cla4_2_gg, cla4_2_pg, cla4_3_gg, cla4_3_pg, cla4_4_gg, cla4_4_pg, clu4_1_c1,
       clu4_1_c2, clu4_1_c3;

  CLA4 cla4_1 (.X(X[15:12]), .F(S[15:12]), .Cout(C16), .Y(Y[15:12]), .Pg(cla4_1_pg), .Cin(clu4_1_c3), .Gg(cla4_1_gg));
  CLU4 clu4_1 (
    .P0(cla4_4_pg), .P1(cla4_3_pg), .P2(cla4_2_pg), .P3(cla4_1_pg), .C1(clu4_1_c1), .C3(clu4_1_c3),
    .G0(cla4_4_gg), .G1(cla4_3_gg), .G2(cla4_2_gg), .G3(cla4_1_gg), .C2(clu4_1_c2), .C0(C0), .Pg(Pg), .Gg(Gg));  // open: C4
  CLA4 cla4_2 (.X(X[11:8]), .F(S[11:8]), .Y(Y[11:8]), .Pg(cla4_2_pg), .Cin(clu4_1_c2), .Gg(cla4_2_gg));  // open: Cout
  CLA4 cla4_3 (.X(X[7:4]), .F(S[7:4]), .Y(Y[7:4]), .Pg(cla4_3_pg), .Cin(clu4_1_c1), .Gg(cla4_3_gg));  // open: Cout
  CLA4 cla4_4 (.X(X[3:0]), .F(S[3:0]), .Y(Y[3:0]), .Pg(cla4_4_pg), .Cin(C0), .Gg(cla4_4_gg));  // open: Cout
  // Probe on X
  // Probe on Y
  // Probe on S

  // Notes on the sheet:
  //   C0: pull=down
  //   X: pull=down
  //   Y: pull=down
  //   输入引脚区
  //   请勿修改引脚名称、电路名称及电路封装外观
  //   提示：使用4位先行进位加法器和CLU子电路实现16位并行加法器
  //   功能说明:16位Adder  S=X+Y，C16为最高位进位位，C0为进位输入， Pg、Gg为成组进位生成传递函数
  //   输出引脚区
  //   +
  //   =
  //   无符号加法
endmodule

module CLA4 (
  input  [3:0] X,
  input  [3:0] Y,
  input  Cin,
  output [3:0] F,
  output Cout,
  output Pg,
  output Gg
);

  wire clu4_1_c1, clu4_1_c2, clu4_1_c3, fa_1_g, fa_1_p, fa_2_g, fa_2_p, fa_3_g, fa_3_p, fa_4_g, fa_4_p;

  FA fa_1 (.A(X[3]), .F(F[3]), .B(Y[3]), .P(fa_1_p), .Cin(clu4_1_c3), .G(fa_1_g));
  Hex_Digit_Display hex_digit_display_1 (.value(X));  // open: dp
  FA fa_2 (.A(X[2]), .F(F[2]), .B(Y[2]), .P(fa_2_p), .Cin(clu4_1_c2), .G(fa_2_g));
  Hex_Digit_Display hex_digit_display_2 (.value(Y));  // open: dp
  CLU4 clu4_1 (
    .P0(fa_4_p), .P1(fa_3_p), .P2(fa_2_p), .P3(fa_1_p), .C1(clu4_1_c1), .C3(clu4_1_c3), .G0(fa_4_g),
    .G1(fa_3_g), .G2(fa_2_g), .G3(fa_1_g), .C2(clu4_1_c2), .C4(Cout), .C0(Cin), .Pg(Pg), .Gg(Gg));
  FA fa_3 (.A(X[1]), .F(F[1]), .B(Y[1]), .P(fa_3_p), .Cin(clu4_1_c1), .G(fa_3_g));
  Hex_Digit_Display hex_digit_display_3 (.value(F));  // open: dp
  FA fa_4 (.A(X[0]), .F(F[0]), .B(Y[0]), .P(fa_4_p), .Cin(Cin), .G(fa_4_g));

  // Other names for the same wires on the sheet: Z[3:0] = F

  // Notes on the sheet:
  //   +
  //   =
  //   输出
  //   输入
  //   请勿修改引脚名称、电路名称及电路封装外观
  //   提示：使用全加器和CLU子电路实现四位先行进位加法器CLA4
endmodule

module CLU4 (
  input  P0,
  input  P1,
  input  P2,
  input  P3,
  input  G0,
  input  G1,
  input  G2,
  input  G3,
  input  C0,
  output C1,
  output C3,
  output C2,
  output C4,
  output Pg,
  output Gg
);

  wire and_1_out, and_3_out, and_4_out, and_5_out, and_6_out, and_7_out, and_8_out, and_9_out, and_10_out,
       and_11_out;

  or or_1 (Gg, G3, and_3_out, and_4_out, and_6_out);
  and and_1 (and_1_out, Pg, C0);
  and and_2 (Pg, P0, P1, P2, P3);
  or or_2 (C4, Gg, and_1_out);
  and and_3 (and_3_out, G0, P1, P2, P3);
  and and_4 (and_4_out, G1, P2, P3);
  or or_3 (C3, G2, and_5_out, and_7_out, and_9_out);
  and and_5 (and_5_out, C0, P0, P1, P2);
  and and_6 (and_6_out, G2, P3);
  and and_7 (and_7_out, G0, P1, P2);
  or or_4 (C2, G1, and_8_out, and_11_out);
  and and_8 (and_8_out, C0, P0, P1);
  and and_9 (and_9_out, G1, P2);
  or or_5 (C1, G0, and_10_out);
  and and_10 (and_10_out, C0, P0);
  and and_11 (and_11_out, G0, P1);

  // Notes on the sheet:
  //   输入引脚
  //   请勿修改引脚名称、电路名称及电路封装外观
  //   提示：使用逻辑门电路实现4位四位先行进位部件CLU，Pg、Gg为成组进位生成传递函数
  //   输出引脚
endmodule

module FA (
  input  A,
  input  B,
  input  Cin,
  output F,
  output P,
  output G
);

  wire xor_1_out;

  and and_1 (G, A, B);
  or or_1 (P, A, B);
  xor xor_1 (xor_1_out, A, B);
  xor xor_2 (F, xor_1_out, Cin);

  // Notes on the sheet:
  //   输入引脚
  //   请勿修改引脚名称、电路名称及电路封装外观
  //   输出引脚
endmodule

module \阻塞检测  (
  input  [6:0] IF_opcode,
  input  [4:0] EX_rd,
  input  [4:0] IF_rs1,
  input  EX_MemtoReg,
  input  [4:0] IF_rs2,
  output Stall
);

  wire and_1_out, and_2_out, and_3_out, and_4_out, comparator_1_eq, comparator_2_eq, comparator_3_eq,
       comparator_4_eq, comparator_5_eq, comparator_6_eq, comparator_7_eq, or_1_out, or_2_out, or_3_out;

  Comparator #(.width(7)) comparator_1 (.a(IF_opcode), .b(7'b0110011), .eq(comparator_1_eq));  // open: gt, lt
  Comparator #(.width(7)) comparator_2 (.a(IF_opcode), .b(7'b0100011), .eq(comparator_2_eq));  // open: gt, lt
  Comparator #(.width(7)) comparator_3 (.a(IF_opcode), .b(7'b1100011), .eq(comparator_3_eq));  // open: gt, lt
  Comparator #(.width(7)) comparator_4 (.a(IF_opcode), .b(7'b0000011), .eq(comparator_4_eq));  // open: gt, lt
  Comparator #(.width(7)) comparator_5 (.a(IF_opcode), .b(7'b0010011), .eq(comparator_5_eq));  // open: gt, lt
  or or_1 (or_1_out, comparator_1_eq, comparator_2_eq, comparator_3_eq);
  or or_2 (or_2_out, or_1_out, or_3_out);
  or or_3 (or_3_out, comparator_4_eq, comparator_5_eq);
  Comparator #(.width(5)) comparator_6 (.a(EX_rd), .b(IF_rs1), .eq(comparator_6_eq));  // open: gt, lt
  Comparator #(.width(5)) comparator_7 (.a(EX_rd), .b(IF_rs2), .eq(comparator_7_eq));  // open: gt, lt
  and and_1 (and_1_out, comparator_7_eq, or_1_out);
  and and_2 (and_2_out, comparator_6_eq, or_2_out);
  and and_3 (and_3_out, and_1_out, EX_MemtoReg);
  and and_4 (and_4_out, and_2_out, EX_MemtoReg);
  or or_4 (Stall, and_3_out, and_4_out);

  // Notes on the sheet:
  //   EX_rd: pull=down
  //   EX_MemtoReg: pull=down
  //   输入信号
  //   输出信号
endmodule

module \转发检测  (
  input  [4:0] EX_rs1,
  input  [4:0] M_rd,
  input  [4:0] EX_rs2,
  input  [4:0] WB_rd,
  input  M_RegWr,
  input  WB_RegWr,
  output [1:0] BusAFW,
  output [1:0] BusBFW
);

  wire and_2_out, and_5_out, comparator_1_eq, comparator_2_eq, comparator_3_eq, comparator_4_eq,
       comparator_5_eq, comparator_6_eq, comparator_7_eq, comparator_8_eq, not_1_out, not_2_out, not_3_out,
       not_4_out;

  Comparator #(.width(5)) comparator_1 (.a(EX_rs1), .b(M_rd), .eq(comparator_1_eq));  // open: gt, lt
  not not_1 (not_1_out, comparator_2_eq);
  Comparator #(.width(5)) comparator_2 (.a({5{1'b0}}), .b(M_rd), .eq(comparator_2_eq));  // open: gt, lt
  Comparator #(.width(5)) comparator_3 (.a(EX_rs1), .b(WB_rd), .eq(comparator_3_eq));  // open: gt, lt
  not not_2 (not_2_out, comparator_4_eq);
  Comparator #(.width(5)) comparator_4 (.a({5{1'b0}}), .b(WB_rd), .eq(comparator_4_eq));  // open: gt, lt
  and and_1 (BusAFW[0], comparator_1_eq, not_1_out, M_RegWr);
  and and_2 (and_2_out, comparator_3_eq, not_2_out, WB_RegWr);
  and and_3 (BusAFW[1], ~BusAFW[0], and_2_out);  // AND_Gate
  Comparator #(.width(5)) comparator_5 (.a(EX_rs2), .b(M_rd), .eq(comparator_5_eq));  // open: gt, lt
  Comparator #(.width(5)) comparator_6 (.a({5{1'b0}}), .b(M_rd), .eq(comparator_6_eq));  // open: gt, lt
  Comparator #(.width(5)) comparator_7 (.a(EX_rs2), .b(WB_rd), .eq(comparator_7_eq));  // open: gt, lt
  Comparator #(.width(5)) comparator_8 (.a({5{1'b0}}), .b(WB_rd), .eq(comparator_8_eq));  // open: gt, lt
  and and_4 (BusBFW[0], comparator_5_eq, not_3_out, M_RegWr);
  not not_3 (not_3_out, comparator_6_eq);
  and and_5 (and_5_out, comparator_7_eq, not_4_out, WB_RegWr);
  not not_4 (not_4_out, comparator_8_eq);
  and and_6 (BusBFW[1], ~BusBFW[0], and_5_out);  // AND_Gate

  // Notes on the sheet:
  //   M_rd: pull=down
  //   WB_rd: pull=down
  //   EX_rs2: pull=down
  //   EX_rs1: pull=down
  //   输入信号
  //   输出信号
endmodule

module \流水段寄存器  (
  input  CLR,
  input  [31:0] PC,
  input  CLK,
  input  WE,
  input  Halt,
  input  [31:0] IR,
  input  [3:0] ALUctr,
  input  ALUASrc,
  input  [1:0] ALUBSrc,
  input  [31:0] BusA,
  input  [2:0] BandJ,
  input  [2:0] MemOp,
  input  MemWr,
  input  [31:0] BusB,
  input  RegWr,
  input  MemtoReg,
  input  [4:0] RD,
  input  [31:0] Imm,
  input  [4:0] RS1,
  input  [4:0] RS2,
  input  Zero,
  input  [31:0] Result,
  input  [31:0] PCTarget,
  input  [31:0] Dout,
  output [31:0] PCo,
  output Halto,
  output [31:0] IRo,
  output [3:0] ALUctro,
  output ALUASrco,
  output [1:0] ALUBSrco,
  output [31:0] BusAo,
  output [2:0] BandJo,
  output [2:0] MemOpo,
  output MemWro,
  output [31:0] BusBo,
  output RegWro,
  output MemtoRego,
  output [4:0] RDo,
  output [31:0] Immo,
  output [4:0] RS1o,
  output [4:0] RS2o,
  output Zeroo,
  output [31:0] Resulto,
  output [31:0] PCTargeto,
  output [31:0] Douto
);

  wire multiplexer_16_out, multiplexer_17_out, multiplexer_18_out, multiplexer_19_out, multiplexer_20_out,
       multiplexer_21_out, or_1_out;
  wire [1:0] multiplexer_15_out;
  wire [2:0] multiplexer_13_out, multiplexer_14_out;
  wire [3:0] multiplexer_9_out;
  wire [4:0] multiplexer_10_out, multiplexer_11_out, multiplexer_12_out;
  wire [31:0] multiplexer_1_out, multiplexer_2_out, multiplexer_3_out, multiplexer_4_out, multiplexer_5_out,
       multiplexer_6_out, multiplexer_7_out, multiplexer_8_out;

  or or_1 (or_1_out, WE, CLR);
  Register #(.width(32), .Select("low")) register_1 (
    .D(multiplexer_1_out), .en(or_1_out), .Q(PCo), .clk(CLK));  // open: clr
  Multiplexer #(.width(32), .enable("false")) multiplexer_1 (
    .in0(PC), .in1({32{1'b0}}), .out(multiplexer_1_out), .sel(CLR));
  Multiplexer #(.width(32), .enable("false")) multiplexer_2 (
    .in0(IR), .in1({32{1'b0}}), .out(multiplexer_2_out), .sel(CLR));
  Register #(.width(32), .Select("low")) register_2 (
    .D(multiplexer_2_out), .en(or_1_out), .Q(IRo), .clk(CLK));  // open: clr
  Register #(.width(32), .Select("low")) register_3 (
    .D(multiplexer_3_out), .en(or_1_out), .Q(BusAo), .clk(CLK));  // open: clr
  Multiplexer #(.width(32), .enable("false")) multiplexer_3 (
    .in0(BusA), .in1({32{1'b0}}), .out(multiplexer_3_out), .sel(CLR));
  Multiplexer #(.width(32), .enable("false")) multiplexer_4 (
    .in0(BusB), .in1({32{1'b0}}), .out(multiplexer_4_out), .sel(CLR));
  Register #(.width(32), .Select("low")) register_4 (
    .D(multiplexer_4_out), .en(or_1_out), .Q(BusBo), .clk(CLK));  // open: clr
  Multiplexer #(.width(32), .enable("false")) multiplexer_5 (
    .in0(Imm), .in1({32{1'b0}}), .out(multiplexer_5_out), .sel(CLR));
  Register #(.width(32), .Select("low")) register_5 (
    .D(multiplexer_5_out), .en(or_1_out), .Q(Immo), .clk(CLK));  // open: clr
  Multiplexer #(.width(32), .enable("false")) multiplexer_6 (
    .in0(Result), .in1({32{1'b0}}), .out(multiplexer_6_out), .sel(CLR));
  Register #(.width(32), .Select("low")) register_6 (
    .D(multiplexer_6_out), .en(or_1_out), .Q(Resulto), .clk(CLK));  // open: clr
  Register #(.width(32), .Select("low")) register_7 (
    .D(multiplexer_7_out), .en(or_1_out), .Q(PCTargeto), .clk(CLK));  // open: clr
  Multiplexer #(.width(32), .enable("false")) multiplexer_7 (
    .in0(PCTarget), .in1({32{1'b0}}), .out(multiplexer_7_out), .sel(CLR));
  Multiplexer #(.width(32), .enable("false")) multiplexer_8 (
    .in0(Dout), .in1({32{1'b0}}), .out(multiplexer_8_out), .sel(CLR));
  Register #(.width(32), .Select("low")) register_8 (
    .D(multiplexer_8_out), .en(or_1_out), .Q(Douto), .clk(CLK));  // open: clr
  Multiplexer #(.width(4), .enable("false")) multiplexer_9 (
    .in0(ALUctr), .in1(4'b0000), .out(multiplexer_9_out), .sel(CLR));
  Multiplexer #(.width(5), .enable("false")) multiplexer_10 (
    .in0(RD), .in1({5{1'b0}}), .out(multiplexer_10_out), .sel(CLR));
  Multiplexer #(.width(5), .enable("false")) multiplexer_11 (
    .in0(RS1), .in1({5{1'b0}}), .out(multiplexer_11_out), .sel(CLR));
  Multiplexer #(.width(5), .enable("false")) multiplexer_12 (
    .in0(RS2), .in1({5{1'b0}}), .out(multiplexer_12_out), .sel(CLR));
  Multiplexer #(.width(3), .enable("false")) multiplexer_13 (
    .in0(BandJ), .in1(3'b000), .out(multiplexer_13_out), .sel(CLR));
  Multiplexer #(.width(3), .enable("false")) multiplexer_14 (
    .in0(MemOp), .in1(3'b000), .out(multiplexer_14_out), .sel(CLR));
  Multiplexer #(.width(2), .enable("false")) multiplexer_15 (
    .in0(ALUBSrc), .in1(2'b00), .out(multiplexer_15_out), .sel(CLR));
  Register #(.width(4), .Select("low")) register_9 (
    .D(multiplexer_9_out), .en(or_1_out), .Q(ALUctro), .clk(CLK));  // open: clr
  Register #(.width(5), .Select("low")) register_10 (
    .D(multiplexer_10_out), .en(or_1_out), .Q(RDo), .clk(CLK));  // open: clr
  Register #(.width(5), .Select("low")) register_11 (
    .D(multiplexer_11_out), .en(or_1_out), .Q(RS1o), .clk(CLK));  // open: clr
  Register #(.width(5), .Select("low")) register_12 (
    .D(multiplexer_12_out), .en(or_1_out), .Q(RS2o), .clk(CLK));  // open: clr
  Register #(.width(3), .Select("low")) register_13 (
    .D(multiplexer_13_out), .en(or_1_out), .Q(BandJo), .clk(CLK));  // open: clr
  Register #(.width(3), .Select("low")) register_14 (
    .D(multiplexer_14_out), .en(or_1_out), .Q(MemOpo), .clk(CLK));  // open: clr
  Register #(.width(2), .Select("low")) register_15 (
    .D(multiplexer_15_out), .en(or_1_out), .Q(ALUBSrco), .clk(CLK));  // open: clr
  Multiplexer #(.enable("false")) multiplexer_16 (.in0(ALUASrc), .in1(1'b0), .out(multiplexer_16_out), .sel(CLR));
  Register #(.width(1), .Select("low")) register_16 (
    .D(multiplexer_16_out), .en(or_1_out), .Q(ALUASrco), .clk(CLK));  // open: clr
  Multiplexer #(.enable("false")) multiplexer_17 (.in0(MemWr), .in1(1'b0), .out(multiplexer_17_out), .sel(CLR));
  Register #(.width(1), .Select("low")) register_17 (
    .D(multiplexer_17_out), .en(or_1_out), .Q(MemWro), .clk(CLK));  // open: clr
  Multiplexer #(.enable("false")) multiplexer_18 (.in0(RegWr), .in1(1'b0), .out(multiplexer_18_out), .sel(CLR));
  Register #(.width(1), .Select("low")) register_18 (
    .D(multiplexer_18_out), .en(or_1_out), .Q(RegWro), .clk(CLK));  // open: clr
  Multiplexer #(.enable("false")) multiplexer_19 (.in0(MemtoReg), .in1(1'b0), .out(multiplexer_19_out), .sel(CLR));
  Register #(.width(1), .Select("low")) register_19 (
    .D(multiplexer_19_out), .en(or_1_out), .Q(MemtoRego), .clk(CLK));  // open: clr
  Register #(.width(1), .Select("low")) register_20 (
    .D(multiplexer_20_out), .en(or_1_out), .Q(Zeroo), .clk(CLK));  // open: clr
  Multiplexer #(.enable("false")) multiplexer_20 (.in0(Zero), .in1(1'b0), .out(multiplexer_20_out), .sel(CLR));
  Register #(.width(1), .Select("low")) register_21 (
    .D(multiplexer_21_out), .en(or_1_out), .Q(Halto), .clk(CLK));  // open: clr
  Multiplexer #(.enable("false")) multiplexer_21 (.in0(Halt), .in1(1'b0), .out(multiplexer_21_out), .sel(CLR));

  // Notes on the sheet:
  //   输入引脚区
  //   输出引脚区
endmodule

module DM (
  input  [15:0] Addr,
  input  [31:0] Din,
  input  CLK,
  input  CLR,
  input  [2:0] MemOp,
  input  WE,
  input  SEL,
  output [31:0] DataOut
);


  // Other names for the same wires on the sheet: Dout[31:0] = DataOut

  // Notes on the sheet:
  //   输入引脚区
  //   32位数据存储器，按字节分4片存储，可按照字节、半字和字进行存储；读取字节或半字时，支持0扩展和符号位扩展。
  //   为了后续实验中的引用，不要修改MemOp的编码定义，以及引脚名称和在布局图中位置。
  //   输出引脚区
endmodule

module EU (
  input  [3:0] ALUctr,
  input  ALUASrc,
  input  [1:0] ALUBSrc,
  input  [31:0] PC,
  input  [31:0] BusA,
  input  [31:0] BusB,
  input  [31:0] Imm,
  input  [2:0] BandJ,
  output [31:0] PCTarget,
  output [31:0] Result,
  output Zero
);


  // Notes on the sheet:
  //   BandJ: pull=down
  //   Result: pull=down
  //   ALUASrc: pull=down
  //   PCTarget: pull=down
  //   ALUctr: pull=down
  //   ALUBSrc: pull=down
  //   输入信号
  //   请勿修改引脚名称、电路名称及电路封装外观
  //   为了后续实验中的引用，不要修改控制信号编码定义。
  //   输出信号
endmodule
